// Logisim project ALU.circ as structural Verilog
module AND_16_Bit (
  input  [15:0] A,
  input  [15:0] B,
  output [15:0] O
);

  and and_1 (O[15], A[15], B[15]);
  and and_2 (O[14], A[14], B[14]);
  and and_3 (O[13], A[13], B[13]);
  and and_4 (O[12], A[12], B[12]);
  and and_5 (O[11], A[11], B[11]);
  and and_6 (O[10], A[10], B[10]);
  and and_7 (O[9], A[9], B[9]);
  and and_8 (O[8], A[8], B[8]);
  and and_9 (O[7], A[7], B[7]);
  and and_10 (O[6], A[6], B[6]);
  and and_11 (O[5], A[5], B[5]);
  and and_12 (O[4], A[4], B[4]);
  and and_13 (O[3], A[3], B[3]);
  and and_14 (O[2], A[2], B[2]);
  and and_15 (O[1], A[1], B[1]);
  and and_16 (O[0], A[0], B[0]);
endmodule

module OR_16_BIT (
  input  [15:0] A,
  input  [15:0] B,
  output [15:0] O
);

  assign O = A | B;  // OR_Gate or_1, 16 bits wide
endmodule

module X0R_16_BIT (
  input  [15:0] A,
  input  [15:0] B,
  output [15:0] O
);

  assign O = A ^ B;  // XOR_Gate xor_1, 16 bits wide
endmodule

module MEMORY_1_BIT (
  input  S,
  output Q
);

  wire nand_1_out, nand_2_out, nand_4_out, not_1_out;

  not not_1 (not_1_out, S);
  nand nand_1 (nand_1_out, 1'b1, not_1_out);
  nand nand_2 (nand_2_out, S, 1'b1);
  nand nand_3 (Q, nand_2_out, nand_4_out);
  nand nand_4 (nand_4_out, Q, nand_1_out);
endmodule

module MEMORY_8_BIT (
  input  [7:0] in_1,
  output [7:0] Q
);

  MEMORY_1_BIT memory_1_bit_1 (.S(in_1[0]), .Q(Q[0]));
  MEMORY_1_BIT memory_1_bit_2 (.S(in_1[1]), .Q(Q[1]));
  MEMORY_1_BIT memory_1_bit_3 (.S(in_1[3]), .Q(Q[3]));
  MEMORY_1_BIT memory_1_bit_4 (.S(in_1[4]), .Q(Q[4]));
  MEMORY_1_BIT memory_1_bit_5 (.S(in_1[5]), .Q(Q[5]));
  MEMORY_1_BIT memory_1_bit_6 (.S(in_1[6]), .Q(Q[6]));
  MEMORY_1_BIT memory_1_bit_7 (.S(in_1[7]), .Q(Q[7]));
  MEMORY_1_BIT memory_1_bit_8 (.S(in_1[2]), .Q(Q[2]));
endmodule

module MEMORY_16_BIT (
  input  [15:0] in_1,
  output [15:0] Q
);

  MEMORY_8_BIT memory_8_bit_1 (.in_1(in_1[7:0]), .Q(Q[7:0]));
  MEMORY_8_BIT memory_8_bit_2 (.in_1(in_1[15:8]), .Q(Q[15:8]));

  // Notes on the sheet:
  //   s
  //   e
  //   s
  //   e
  //   Q
  //   Q
endmodule

module SHIFT_LEFT (
  input  [15:0] Inputs,
  output [15:0] Outputs,
  output Overflow
);

  MEMORY_16_BIT memory_16_bit_1 (.in_1(Inputs), .Q({Overflow, Outputs[15:1]}));

  assign Outputs[0] = 1'b0;

  // Notes on the sheet:
  //   s
  //   e
  //   Q
endmodule

module SHIFT_RIGHT (
  input  [15:0] Inputs,
  output Underflow,
  output [15:0] Outputs
);

  MEMORY_16_BIT memory_16_bit_1 (.in_1(Inputs), .Q({Outputs[14:0], Underflow}));

  assign Outputs[15] = 1'b0;

  // Notes on the sheet:
  //   s
  //   e
  //   Q
endmodule

module CIRCULAR_LEFT_SHIFT (
  input  [15:0] Inputs,
  output [15:0] Outputs
);

  MEMORY_16_BIT memory_16_bit_1 (.in_1(Inputs), .Q({Outputs[0], Outputs[15:1]}));

  // Notes on the sheet:
  //   s
  //   e
  //   Q
endmodule

module CIRCULAR_RIGHT_SHIFT (
  input  [15:0] Inputs,
  output [15:0] Outputus
);

  MEMORY_16_BIT memory_16_bit_1 (.in_1(Inputs), .Q({Outputus[14:0], Outputus[15]}));

  // Notes on the sheet:
  //   s
  //   e
  //   Q
endmodule

module DIVISION_16_BIT (
  input  [15:0] a,
  input  [15:0] b,
  output [15:0] quotient_output,
  output carry_undefined
);

  wire or_1_out;
  wire [15:0] divider_1_out;

  Divider #(.width(16)) divider_1 (.a(a), .b(b), .out(divider_1_out));  // open: upper, rem
  or or_1 (or_1_out, b[0], b[1], b[2], b[3], b[4], b[5], b[6], b[7], b[8], b[9], b[10], b[11], b[12], b[13], b[14], b[15]);
  and and_1 (quotient_output[0], divider_1_out[0], or_1_out);
  and and_2 (quotient_output[1], divider_1_out[1], or_1_out);
  and and_3 (quotient_output[2], divider_1_out[2], or_1_out);
  and and_4 (quotient_output[3], divider_1_out[3], or_1_out);
  and and_5 (quotient_output[4], divider_1_out[4], or_1_out);
  and and_6 (quotient_output[5], divider_1_out[5], or_1_out);
  and and_7 (quotient_output[6], divider_1_out[6], or_1_out);
  and and_8 (quotient_output[7], divider_1_out[7], or_1_out);
  and and_9 (quotient_output[8], divider_1_out[8], or_1_out);
  and and_10 (quotient_output[9], divider_1_out[9], or_1_out);
  and and_11 (quotient_output[10], divider_1_out[10], or_1_out);
  and and_12 (quotient_output[11], divider_1_out[11], or_1_out);
  and and_13 (quotient_output[12], divider_1_out[12], or_1_out);
  and and_14 (quotient_output[13], divider_1_out[13], or_1_out);
  and and_15 (quotient_output[14], divider_1_out[14], or_1_out);
  and and_16 (quotient_output[15], or_1_out, divider_1_out[15]);
  not not_1 (carry_undefined, or_1_out);
endmodule

module MODULO_16_BIT (
  input  [15:0] a,
  input  [15:0] b,
  output [15:0] modulo_output
);

  Divider #(.width(16)) divider_1 (.a(a), .b(b), .rem(modulo_output));  // open: out, upper
endmodule

module INCREMENT_16_BIT (
  input  [15:0] a,
  output [15:0] output_inc,
  output carry_inc
);

  Adder #(.width(16)) adder_1 (.a(a), .b(16'h1), .out(output_inc), .cout(carry_inc));  // open: cin
endmodule

module DECREMENT_16_BIT (
  input  [15:0] a,
  output [15:0] output_decrement,
  output carry_dec
);

  Subtractor #(.width(16)) subtractor_1 (.a(a), .b(16'h1), .out(output_decrement), .bout(carry_dec));  // open: bin
endmodule

module MULTIPLICATION_16_BIT (
  input  [15:0] a,
  input  [15:0] b,
  output [15:0] output_mul,
  output invalid_flag
);

  wire or_1_out, or_2_out;

  Multiplier multiplier_1 (.a(a[7:0]), .b(b[7:0]), .out(output_mul[7:0]), .cout(output_mul[15:8]));  // open: cin
  or or_1 (or_1_out, a[8], a[9], a[10], a[11], a[12], a[13], a[14], a[15]);
  or or_2 (or_2_out, b[15], b[14], b[13], b[12], b[11], b[10], b[9], b[8]);
  or or_3 (invalid_flag, or_2_out, or_1_out);
endmodule

module FULL_ADDER_16_BIT (
  input  [15:0] A,
  input  [15:0] B,
  input  Cin,
  output [15:0] S,
  output Cout
);

  wire adder_1_bit_1_cout, adder_1_bit_2_cout, adder_1_bit_3_cout, adder_1_bit_4_cout, adder_1_bit_5_cout,
       adder_1_bit_6_cout, adder_1_bit_7_cout, adder_1_bit_8_cout, adder_1_bit_9_cout, adder_1_bit_10_cout,
       adder_1_bit_11_cout, adder_1_bit_12_cout, adder_1_bit_13_cout, adder_1_bit_14_cout,
       adder_1_bit_15_cout, undriven;

  ADDER_1_BIT adder_1_bit_1 (.Cin(undriven), .A(A[0]), .B(B[0]), .Sum(S[0]), .Cout(adder_1_bit_1_cout));
  ADDER_1_BIT adder_1_bit_2 (.Cin(adder_1_bit_1_cout), .A(A[1]), .B(B[1]), .Sum(S[1]), .Cout(adder_1_bit_2_cout));
  ADDER_1_BIT adder_1_bit_3 (.Cin(adder_1_bit_2_cout), .A(A[2]), .B(B[2]), .Sum(S[2]), .Cout(adder_1_bit_3_cout));
  ADDER_1_BIT adder_1_bit_4 (.Cin(adder_1_bit_3_cout), .A(A[3]), .B(B[3]), .Sum(S[3]), .Cout(adder_1_bit_4_cout));
  ADDER_1_BIT adder_1_bit_5 (.Cin(adder_1_bit_4_cout), .A(A[4]), .B(B[4]), .Sum(S[4]), .Cout(adder_1_bit_5_cout));
  ADDER_1_BIT adder_1_bit_6 (.Cin(adder_1_bit_5_cout), .A(A[5]), .B(B[5]), .Sum(S[5]), .Cout(adder_1_bit_6_cout));
  ADDER_1_BIT adder_1_bit_7 (.Cin(adder_1_bit_6_cout), .A(A[6]), .B(B[6]), .Sum(S[6]), .Cout(adder_1_bit_7_cout));
  ADDER_1_BIT adder_1_bit_8 (.Cin(adder_1_bit_7_cout), .A(A[7]), .B(B[7]), .Sum(S[7]), .Cout(adder_1_bit_8_cout));
  ADDER_1_BIT adder_1_bit_9 (.Cin(adder_1_bit_8_cout), .A(A[8]), .B(B[8]), .Sum(S[8]), .Cout(adder_1_bit_9_cout));
  ADDER_1_BIT adder_1_bit_10 (.Cin(adder_1_bit_9_cout), .A(A[9]), .B(B[9]), .Sum(S[9]), .Cout(adder_1_bit_10_cout));
  ADDER_1_BIT adder_1_bit_11 (.Cin(adder_1_bit_10_cout), .A(A[10]), .B(B[10]), .Sum(S[10]), .Cout(adder_1_bit_11_cout));
  ADDER_1_BIT adder_1_bit_12 (.Cin(adder_1_bit_11_cout), .A(A[11]), .B(B[11]), .Sum(S[11]), .Cout(adder_1_bit_12_cout));
  ADDER_1_BIT adder_1_bit_13 (.Cin(adder_1_bit_12_cout), .A(A[12]), .B(B[12]), .Sum(S[12]), .Cout(adder_1_bit_13_cout));
  ADDER_1_BIT adder_1_bit_14 (.Cin(adder_1_bit_13_cout), .A(A[13]), .B(B[13]), .Sum(S[13]), .Cout(adder_1_bit_14_cout));
  ADDER_1_BIT adder_1_bit_15 (.Cin(adder_1_bit_14_cout), .A(A[14]), .B(B[14]), .Sum(S[14]), .Cout(adder_1_bit_15_cout));
  ADDER_1_BIT adder_1_bit_16 (.Cin(adder_1_bit_15_cout), .A(A[15]), .B(B[15]), .Sum(S[15]), .Cout(Cout));
endmodule

module ADDER_1_BIT (
  input  Cin,
  input  A,
  input  B,
  output Sum,
  output Cout
);

  wire and_1_out, and_2_out, xor_1_out;

  xor xor_1 (xor_1_out, A, B);
  and and_1 (and_1_out, xor_1_out, Cin);
  and and_2 (and_2_out, A, B);
  xor xor_2 (Sum, Cin, xor_1_out);
  or or_1 (Cout, and_1_out, and_2_out);
endmodule

module ADD_WITHOUT_CARRY_16_BITS (
  input  [15:0] A,
  input  [15:0] B,
  output [15:0] S,
  output Cout
);

  wire adder_1_bit_1_cout, adder_1_bit_2_cout, adder_1_bit_3_cout, adder_1_bit_4_cout, adder_1_bit_5_cout,
       adder_1_bit_6_cout, adder_1_bit_7_cout, adder_1_bit_8_cout, adder_1_bit_9_cout, adder_1_bit_10_cout,
       adder_1_bit_11_cout, adder_1_bit_12_cout, adder_1_bit_13_cout, adder_1_bit_14_cout,
       adder_1_bit_15_cout;

  ADDER_1_BIT adder_1_bit_1 (.Cin(1'b0), .A(A[0]), .B(B[0]), .Sum(S[0]), .Cout(adder_1_bit_1_cout));
  ADDER_1_BIT adder_1_bit_2 (.Cin(adder_1_bit_1_cout), .A(A[1]), .B(B[1]), .Sum(S[1]), .Cout(adder_1_bit_2_cout));
  ADDER_1_BIT adder_1_bit_3 (.Cin(adder_1_bit_2_cout), .A(A[2]), .B(B[2]), .Sum(S[2]), .Cout(adder_1_bit_3_cout));
  ADDER_1_BIT adder_1_bit_4 (.Cin(adder_1_bit_3_cout), .A(A[3]), .B(B[3]), .Sum(S[3]), .Cout(adder_1_bit_4_cout));
  ADDER_1_BIT adder_1_bit_5 (.Cin(adder_1_bit_4_cout), .A(A[4]), .B(B[4]), .Sum(S[4]), .Cout(adder_1_bit_5_cout));
  ADDER_1_BIT adder_1_bit_6 (.Cin(adder_1_bit_5_cout), .A(A[5]), .B(B[5]), .Sum(S[5]), .Cout(adder_1_bit_6_cout));
  ADDER_1_BIT adder_1_bit_7 (.Cin(adder_1_bit_6_cout), .A(A[6]), .B(B[6]), .Sum(S[6]), .Cout(adder_1_bit_7_cout));
  ADDER_1_BIT adder_1_bit_8 (.Cin(adder_1_bit_7_cout), .A(A[7]), .B(B[7]), .Sum(S[7]), .Cout(adder_1_bit_8_cout));
  ADDER_1_BIT adder_1_bit_9 (.Cin(adder_1_bit_8_cout), .A(A[8]), .B(B[8]), .Sum(S[8]), .Cout(adder_1_bit_9_cout));
  ADDER_1_BIT adder_1_bit_10 (.Cin(adder_1_bit_9_cout), .A(A[9]), .B(B[9]), .Sum(S[9]), .Cout(adder_1_bit_10_cout));
  ADDER_1_BIT adder_1_bit_11 (.Cin(adder_1_bit_10_cout), .A(A[10]), .B(B[10]), .Sum(S[10]), .Cout(adder_1_bit_11_cout));
  ADDER_1_BIT adder_1_bit_12 (.Cin(adder_1_bit_11_cout), .A(A[11]), .B(B[11]), .Sum(S[11]), .Cout(adder_1_bit_12_cout));
  ADDER_1_BIT adder_1_bit_13 (.Cin(adder_1_bit_12_cout), .A(A[12]), .B(B[12]), .Sum(S[12]), .Cout(adder_1_bit_13_cout));
  ADDER_1_BIT adder_1_bit_14 (.Cin(adder_1_bit_13_cout), .A(A[13]), .B(B[13]), .Sum(S[13]), .Cout(adder_1_bit_14_cout));
  ADDER_1_BIT adder_1_bit_15 (.Cin(adder_1_bit_14_cout), .A(A[14]), .B(B[14]), .Sum(S[14]), .Cout(adder_1_bit_15_cout));
  ADDER_1_BIT adder_1_bit_16 (.Cin(adder_1_bit_15_cout), .A(A[15]), .B(B[15]), .Sum(S[15]), .Cout(Cout));
endmodule

module ALU_final (
  input  C_IN,
  input  [15:0] a,
  input  [15:0] b,
  input  [3:0] opcode,
  output [15:0] output_of_operation_xxxx,
  output undefined_status_flag,
  output overflow_flag,
  output underflow_flag,
  output negative_overflow
);

  wire add_without_carry_16_bits_1_cout, decrement_16_bit_1_carry_dec, division_16_bit_1_carry_undefined,
       full_adder_16_bit_1_cout, increment_16_bit_1_carry_inc, multiplication_16_bit_1_invalid_flag,
       shift_left_1_overflow, shift_right_1_underflow, subtractor_16bit_1_bout,
       subtractor_16bit_1_negative_overflow, subtractor_without_borrow_1_bout,
       subtractor_without_borrow_1_negative_overflow;
  wire [15:0] add_without_carry_16_bits_1_s, and_16_bit_1_o, circular_left_shift_1_outputs,
       circular_right_shift_1_outputus, decrement_16_bit_1_output_decrement,
       division_16_bit_1_quotient_output, full_adder_16_bit_1_s, increment_16_bit_1_output_inc,
       modulo_16_bit_1_modulo_output, multiplication_16_bit_1_output_mul, or_16_bit_1_o,
       shift_left_1_outputs, shift_right_1_outputs, subtractor_16bit_1_difference,
       subtractor_without_borrow_1_difference, x0r_16_bit_1_o;

  SUBTRACTOR_WITHOUT_BORROW subtractor_without_borrow_1 (
    .B(b), .A(a), .Difference(subtractor_without_borrow_1_difference),
    .negative_overflow(subtractor_without_borrow_1_negative_overflow), .Bout(subtractor_without_borrow_1_bout));
  AND_16_Bit and_16_bit_1 (.A(a), .B(b), .O(and_16_bit_1_o));
  OR_16_BIT or_16_bit_1 (.A(a), .B(b), .O(or_16_bit_1_o));
  X0R_16_BIT x0r_16_bit_1 (.A(a), .B(b), .O(x0r_16_bit_1_o));
  SHIFT_LEFT shift_left_1 (.Inputs(a), .Outputs(shift_left_1_outputs), .Overflow(shift_left_1_overflow));
  SHIFT_RIGHT shift_right_1 (.Inputs(a), .Underflow(shift_right_1_underflow), .Outputs(shift_right_1_outputs));
  CIRCULAR_LEFT_SHIFT circular_left_shift_1 (.Inputs(a), .Outputs(circular_left_shift_1_outputs));
  CIRCULAR_RIGHT_SHIFT circular_right_shift_1 (.Inputs(a), .Outputus(circular_right_shift_1_outputus));
  DIVISION_16_BIT division_16_bit_1 (
    .a(a), .b(b), .quotient_output(division_16_bit_1_quotient_output),
    .carry_undefined(division_16_bit_1_carry_undefined));
  MODULO_16_BIT modulo_16_bit_1 (.a(a), .b(b), .modulo_output(modulo_16_bit_1_modulo_output));
  INCREMENT_16_BIT increment_16_bit_1 (
    .a(a), .output_inc(increment_16_bit_1_output_inc), .carry_inc(increment_16_bit_1_carry_inc));
  DECREMENT_16_BIT decrement_16_bit_1 (
    .a(a), .output_decrement(decrement_16_bit_1_output_decrement), .carry_dec(decrement_16_bit_1_carry_dec));
  MULTIPLICATION_16_BIT multiplication_16_bit_1 (
    .a(a), .b(b), .output_mul(multiplication_16_bit_1_output_mul),
    .invalid_flag(multiplication_16_bit_1_invalid_flag));
  FULL_ADDER_16_BIT full_adder_16_bit_1 (
    .A(a), .B(b), .Cin(C_IN), .S(full_adder_16_bit_1_s), .Cout(full_adder_16_bit_1_cout));
  ADD_WITHOUT_CARRY_16_BITS add_without_carry_16_bits_1 (
    .A(a), .B(b), .S(add_without_carry_16_bits_1_s), .Cout(add_without_carry_16_bits_1_cout));
  SUBTRACTOR_16BIT subtractor_16bit_1 (
    .B(b), .A(a), .Bin(C_IN), .Difference(subtractor_16bit_1_difference),
    .negative_overflow(subtractor_16bit_1_negative_overflow), .Bout(subtractor_16bit_1_bout));
  Multiplexer #(.select(4), .width(16)) multiplexer_1 (
    .in0(and_16_bit_1_o), .in1(or_16_bit_1_o), .in2(x0r_16_bit_1_o), .in3(shift_left_1_outputs),
    .in4(shift_right_1_outputs), .in5(circular_left_shift_1_outputs), .in6(circular_right_shift_1_outputus),
    .in7(division_16_bit_1_quotient_output), .in8(modulo_16_bit_1_modulo_output),
    .in9(increment_16_bit_1_output_inc), .in10(decrement_16_bit_1_output_decrement),
    .in11(multiplication_16_bit_1_output_mul), .in12(full_adder_16_bit_1_s),
    .in13(add_without_carry_16_bits_1_s), .in14(subtractor_16bit_1_difference),
    .in15(subtractor_without_borrow_1_difference), .out(output_of_operation_xxxx), .sel(opcode));
  Multiplexer #(.select(4)) multiplexer_2 (
    .in3(shift_left_1_overflow), .in9(increment_16_bit_1_carry_inc), .in10(decrement_16_bit_1_carry_dec),
    .in11(multiplication_16_bit_1_invalid_flag), .in12(full_adder_16_bit_1_cout),
    .in13(add_without_carry_16_bits_1_cout), .out(overflow_flag), .sel(opcode));  // open: in0, in1, in2, in4, in5, in6, in7, in8, in14, in15
  Multiplexer #(.select(4)) multiplexer_3 (
    .in4(shift_right_1_underflow), .out(underflow_flag), .sel(opcode));  // open: in0, in1, in2, in3, in5, in6, in7, in8, in9, in10, in11, in12, in13, in14, in15
  Multiplexer #(.select(4)) multiplexer_4 (
    .in7(division_16_bit_1_carry_undefined), .out(undefined_status_flag), .sel(opcode));  // open: in0, in1, in2, in3, in4, in5, in6, in8, in9, in10, in11, in12, in13, in14, in15
  Multiplexer #(.select(4)) multiplexer_5 (
    .in14(subtractor_16bit_1_negative_overflow), .in15(subtractor_without_borrow_1_negative_overflow),
    .out(negative_overflow), .sel(opcode));  // open: in0, in1, in2, in3, in4, in5, in6, in7, in8, in9, in10, in11, in12, in13
  // also tied to GND on the sheet: {subtractor_without_borrow_1_bout, subtractor_16bit_1_bout}

  // Notes on the sheet:
  //   2. check what the bout means at the end of the day
  //   Arithmetic and Logic Unit of our Microprocessor
endmodule

module ALU_testing (
  input  in_1,
  input  [15:0] in_2,
  input  [15:0] in_3,
  input  [3:0] in_4,
  output [15:0] out_5,
  output out_6,
  output out_7,
  output out_8,
  output out_9
);

  ALU_final alu_final_1 (
    .C_IN(in_1), .a(in_2), .b(in_3), .opcode(in_4), .output_of_operation_xxxx(out_5),
    .undefined_status_flag(out_6), .overflow_flag(out_7), .underflow_flag(out_8), .negative_overflow(out_9));

  // Notes on the sheet:
  //   OP-CODE
  //   0000
  //   0001
  //   0010
  //   0011
  //   0100
  //   0101
  //   0110
  //   0111
  //   1000
  //   1001
  //   1010
  //   1011
  //   1100
  //   1101
  //   1110
  //   1111
  //   Register File
  //   INSTRUCTION
  //   AND OPERATION
  //   OR OPERATION
  //   XOR OPERATION
  //   SHIFT LEFT OPERATION
  //   SHIFT RIGHT OPERATION
  //   CIRCULAR LEFT SHIFT OPERATION
  //   CIRCULAR RIGHT SHIFT OPERATION
  //   DIVISION OPERATION
  //   MODULO OPERATION
  //   INCREMENT OPERATION
  //   DECREMENT OPERATION
  //   MULTIPLICATION OPERATION
  //   ADD WITH CARRY-IN
  //   ADD OPERATION
  //   SUBTRACT WITH BORROW-IN
  //   SUBTRACT OPERATION
  //   Multiplication is 8 bit by 8 bit multiplication. So, your multiplication should be 00000000xxxxxxxx times 00000000xxxxxxxx
endmodule

module SUBTRACTOR_1BIT (
  input  A,
  input  B,
  input  Bin,
  output D,
  output Bout
);

  wire and_1_out, and_2_out, and_3_out, not_1_out, xor_1_out;

  not not_1 (not_1_out, A);
  and and_1 (and_1_out, not_1_out, B);
  and and_2 (and_2_out, B, Bin);
  and and_3 (and_3_out, not_1_out, Bin);
  xor xor_1 (xor_1_out, A, B);
  xor xor_2 (D, xor_1_out, Bin);
  or or_1 (Bout, and_1_out, and_3_out, and_2_out);
endmodule

module SUBTRACTOR_16BIT (
  input  [15:0] B,
  input  [15:0] A,
  input  Bin,
  output [15:0] Difference,
  output negative_overflow,
  output Bout
);

  wire comparator_1_lt, not_1_out, subtractor_1bit_1_bout, subtractor_1bit_1_d, subtractor_1bit_2_bout,
       subtractor_1bit_2_d, subtractor_1bit_3_bout, subtractor_1bit_3_d, subtractor_1bit_4_bout,
       subtractor_1bit_4_d, subtractor_1bit_5_bout, subtractor_1bit_5_d, subtractor_1bit_6_bout,
       subtractor_1bit_6_d, subtractor_1bit_7_bout, subtractor_1bit_7_d, subtractor_1bit_8_bout,
       subtractor_1bit_8_d, subtractor_1bit_9_bout, subtractor_1bit_9_d, subtractor_1bit_10_bout,
       subtractor_1bit_10_d, subtractor_1bit_11_bout, subtractor_1bit_11_d, subtractor_1bit_12_bout,
       subtractor_1bit_12_d, subtractor_1bit_13_bout, subtractor_1bit_13_d, subtractor_1bit_14_bout,
       subtractor_1bit_14_d, subtractor_1bit_15_bout, subtractor_1bit_15_d, subtractor_1bit_16_d;

  Comparator #(.width(16)) comparator_1 (.a(A), .b(B), .lt(comparator_1_lt));  // open: gt, eq
  not not_1 (not_1_out, comparator_1_lt);
  SUBTRACTOR_1BIT subtractor_1bit_1 (
    .A(A[0]), .B(B[0]), .Bin(Bin), .D(subtractor_1bit_1_d), .Bout(subtractor_1bit_1_bout));
  SUBTRACTOR_1BIT subtractor_1bit_2 (
    .A(A[1]), .B(B[1]), .Bin(subtractor_1bit_1_bout), .D(subtractor_1bit_2_d), .Bout(subtractor_1bit_2_bout));
  SUBTRACTOR_1BIT subtractor_1bit_3 (
    .A(A[2]), .B(B[2]), .Bin(subtractor_1bit_2_bout), .D(subtractor_1bit_3_d), .Bout(subtractor_1bit_3_bout));
  SUBTRACTOR_1BIT subtractor_1bit_4 (
    .A(A[3]), .B(B[3]), .Bin(subtractor_1bit_3_bout), .D(subtractor_1bit_4_d), .Bout(subtractor_1bit_4_bout));
  SUBTRACTOR_1BIT subtractor_1bit_5 (
    .A(A[4]), .B(B[4]), .Bin(subtractor_1bit_4_bout), .D(subtractor_1bit_5_d), .Bout(subtractor_1bit_5_bout));
  SUBTRACTOR_1BIT subtractor_1bit_6 (
    .A(A[5]), .B(B[5]), .Bin(subtractor_1bit_5_bout), .D(subtractor_1bit_6_d), .Bout(subtractor_1bit_6_bout));
  SUBTRACTOR_1BIT subtractor_1bit_7 (
    .A(A[6]), .B(B[6]), .Bin(subtractor_1bit_6_bout), .D(subtractor_1bit_7_d), .Bout(subtractor_1bit_7_bout));
  SUBTRACTOR_1BIT subtractor_1bit_8 (
    .A(A[7]), .B(B[7]), .Bin(subtractor_1bit_7_bout), .D(subtractor_1bit_8_d), .Bout(subtractor_1bit_8_bout));
  SUBTRACTOR_1BIT subtractor_1bit_9 (
    .A(A[8]), .B(B[8]), .Bin(subtractor_1bit_8_bout), .D(subtractor_1bit_9_d), .Bout(subtractor_1bit_9_bout));
  SUBTRACTOR_1BIT subtractor_1bit_10 (
    .A(A[9]), .B(B[9]), .Bin(subtractor_1bit_9_bout), .D(subtractor_1bit_10_d), .Bout(subtractor_1bit_10_bout));
  SUBTRACTOR_1BIT subtractor_1bit_11 (
    .A(A[10]), .B(B[10]), .Bin(subtractor_1bit_10_bout), .D(subtractor_1bit_11_d),
    .Bout(subtractor_1bit_11_bout));
  SUBTRACTOR_1BIT subtractor_1bit_12 (
    .A(A[11]), .B(B[11]), .Bin(subtractor_1bit_11_bout), .D(subtractor_1bit_12_d),
    .Bout(subtractor_1bit_12_bout));
  SUBTRACTOR_1BIT subtractor_1bit_13 (
    .A(A[12]), .B(B[12]), .Bin(subtractor_1bit_12_bout), .D(subtractor_1bit_13_d),
    .Bout(subtractor_1bit_13_bout));
  SUBTRACTOR_1BIT subtractor_1bit_14 (
    .A(A[13]), .B(B[13]), .Bin(subtractor_1bit_13_bout), .D(subtractor_1bit_14_d),
    .Bout(subtractor_1bit_14_bout));
  SUBTRACTOR_1BIT subtractor_1bit_15 (
    .A(A[14]), .B(B[14]), .Bin(subtractor_1bit_14_bout), .D(subtractor_1bit_15_d),
    .Bout(subtractor_1bit_15_bout));
  SUBTRACTOR_1BIT subtractor_1bit_16 (
    .A(A[15]), .B(B[15]), .Bin(subtractor_1bit_15_bout), .D(subtractor_1bit_16_d), .Bout(Bout));
  not not_2 (negative_overflow, not_1_out);
  and and_1 (Difference[0], not_1_out, subtractor_1bit_1_d);
  and and_2 (Difference[1], not_1_out, subtractor_1bit_2_d);
  and and_3 (Difference[2], not_1_out, subtractor_1bit_3_d);
  and and_4 (Difference[3], not_1_out, subtractor_1bit_4_d);
  and and_5 (Difference[4], not_1_out, subtractor_1bit_5_d);
  and and_6 (Difference[5], not_1_out, subtractor_1bit_6_d);
  and and_7 (Difference[6], not_1_out, subtractor_1bit_7_d);
  and and_8 (Difference[7], not_1_out, subtractor_1bit_8_d);
  and and_9 (Difference[8], not_1_out, subtractor_1bit_9_d);
  and and_10 (Difference[9], not_1_out, subtractor_1bit_10_d);
  and and_11 (Difference[10], not_1_out, subtractor_1bit_11_d);
  and and_12 (Difference[11], not_1_out, subtractor_1bit_12_d);
  and and_13 (Difference[12], not_1_out, subtractor_1bit_13_d);
  and and_14 (Difference[13], not_1_out, subtractor_1bit_14_d);
  and and_15 (Difference[14], not_1_out, subtractor_1bit_15_d);
  and and_16 (Difference[15], not_1_out, subtractor_1bit_16_d);
endmodule

module SUBTRACTOR_WITHOUT_BORROW (
  input  [15:0] B,
  input  [15:0] A,
  output [15:0] Difference,
  output negative_overflow,
  output Bout
);

  wire comparator_1_eq, comparator_1_gt, comparator_1_lt, not_1_out, subtractor_1bit_1_bout,
       subtractor_1bit_1_d, subtractor_1bit_2_bout, subtractor_1bit_2_d, subtractor_1bit_3_bout,
       subtractor_1bit_3_d, subtractor_1bit_4_bout, subtractor_1bit_4_d, subtractor_1bit_5_bout,
       subtractor_1bit_5_d, subtractor_1bit_6_bout, subtractor_1bit_6_d, subtractor_1bit_7_bout,
       subtractor_1bit_7_d, subtractor_1bit_8_bout, subtractor_1bit_8_d, subtractor_1bit_9_bout,
       subtractor_1bit_9_d, subtractor_1bit_10_bout, subtractor_1bit_10_d, subtractor_1bit_11_bout,
       subtractor_1bit_11_d, subtractor_1bit_12_bout, subtractor_1bit_12_d, subtractor_1bit_13_bout,
       subtractor_1bit_13_d, subtractor_1bit_14_bout, subtractor_1bit_14_d, subtractor_1bit_15_bout,
       subtractor_1bit_15_d, subtractor_1bit_16_d;

  Comparator #(.mode("unsigned"), .width(16)) comparator_1 (
    .a(A), .b(B), .gt(comparator_1_gt), .eq(comparator_1_eq), .lt(comparator_1_lt));
  not not_1 (not_1_out, comparator_1_lt);
  SUBTRACTOR_1BIT subtractor_1bit_1 (
    .A(A[0]), .B(B[0]), .Bin(1'b0), .D(subtractor_1bit_1_d), .Bout(subtractor_1bit_1_bout));
  SUBTRACTOR_1BIT subtractor_1bit_2 (
    .A(A[1]), .B(B[1]), .Bin(subtractor_1bit_1_bout), .D(subtractor_1bit_2_d), .Bout(subtractor_1bit_2_bout));
  SUBTRACTOR_1BIT subtractor_1bit_3 (
    .A(A[2]), .B(B[2]), .Bin(subtractor_1bit_2_bout), .D(subtractor_1bit_3_d), .Bout(subtractor_1bit_3_bout));
  SUBTRACTOR_1BIT subtractor_1bit_4 (
    .A(A[3]), .B(B[3]), .Bin(subtractor_1bit_3_bout), .D(subtractor_1bit_4_d), .Bout(subtractor_1bit_4_bout));
  SUBTRACTOR_1BIT subtractor_1bit_5 (
    .A(A[4]), .B(B[4]), .Bin(subtractor_1bit_4_bout), .D(subtractor_1bit_5_d), .Bout(subtractor_1bit_5_bout));
  SUBTRACTOR_1BIT subtractor_1bit_6 (
    .A(A[5]), .B(B[5]), .Bin(subtractor_1bit_5_bout), .D(subtractor_1bit_6_d), .Bout(subtractor_1bit_6_bout));
  SUBTRACTOR_1BIT subtractor_1bit_7 (
    .A(A[6]), .B(B[6]), .Bin(subtractor_1bit_6_bout), .D(subtractor_1bit_7_d), .Bout(subtractor_1bit_7_bout));
  SUBTRACTOR_1BIT subtractor_1bit_8 (
    .A(A[7]), .B(B[7]), .Bin(subtractor_1bit_7_bout), .D(subtractor_1bit_8_d), .Bout(subtractor_1bit_8_bout));
  SUBTRACTOR_1BIT subtractor_1bit_9 (
    .A(A[8]), .B(B[8]), .Bin(subtractor_1bit_8_bout), .D(subtractor_1bit_9_d), .Bout(subtractor_1bit_9_bout));
  SUBTRACTOR_1BIT subtractor_1bit_10 (
    .A(A[9]), .B(B[9]), .Bin(subtractor_1bit_9_bout), .D(subtractor_1bit_10_d), .Bout(subtractor_1bit_10_bout));
  SUBTRACTOR_1BIT subtractor_1bit_11 (
    .A(A[10]), .B(B[10]), .Bin(subtractor_1bit_10_bout), .D(subtractor_1bit_11_d),
    .Bout(subtractor_1bit_11_bout));
  SUBTRACTOR_1BIT subtractor_1bit_12 (
    .A(A[11]), .B(B[11]), .Bin(subtractor_1bit_11_bout), .D(subtractor_1bit_12_d),
    .Bout(subtractor_1bit_12_bout));
  SUBTRACTOR_1BIT subtractor_1bit_13 (
    .A(A[12]), .B(B[12]), .Bin(subtractor_1bit_12_bout), .D(subtractor_1bit_13_d),
    .Bout(subtractor_1bit_13_bout));
  SUBTRACTOR_1BIT subtractor_1bit_14 (
    .A(A[13]), .B(B[13]), .Bin(subtractor_1bit_13_bout), .D(subtractor_1bit_14_d),
    .Bout(subtractor_1bit_14_bout));
  SUBTRACTOR_1BIT subtractor_1bit_15 (
    .A(A[14]), .B(B[14]), .Bin(subtractor_1bit_14_bout), .D(subtractor_1bit_15_d),
    .Bout(subtractor_1bit_15_bout));
  SUBTRACTOR_1BIT subtractor_1bit_16 (
    .A(A[15]), .B(B[15]), .Bin(subtractor_1bit_15_bout), .D(subtractor_1bit_16_d), .Bout(Bout));
  not not_2 (negative_overflow, not_1_out);
  and and_1 (Difference[0], not_1_out, subtractor_1bit_1_d);
  and and_2 (Difference[1], not_1_out, subtractor_1bit_2_d);
  and and_3 (Difference[2], not_1_out, subtractor_1bit_3_d);
  and and_4 (Difference[3], not_1_out, subtractor_1bit_4_d);
  and and_5 (Difference[4], not_1_out, subtractor_1bit_5_d);
  and and_6 (Difference[5], not_1_out, subtractor_1bit_6_d);
  and and_7 (Difference[6], not_1_out, subtractor_1bit_7_d);
  and and_8 (Difference[7], not_1_out, subtractor_1bit_8_d);
  and and_9 (Difference[8], not_1_out, subtractor_1bit_9_d);
  and and_10 (Difference[9], not_1_out, subtractor_1bit_10_d);
  and and_11 (Difference[10], not_1_out, subtractor_1bit_11_d);
  and and_12 (Difference[11], not_1_out, subtractor_1bit_12_d);
  and and_13 (Difference[12], not_1_out, subtractor_1bit_13_d);
  and and_14 (Difference[13], not_1_out, subtractor_1bit_14_d);
  and and_15 (Difference[14], not_1_out, subtractor_1bit_15_d);
  and and_16 (Difference[15], not_1_out, subtractor_1bit_16_d);
endmodule
