// Logisim project CPU_MICROPROCESSOR.circ as structural Verilog: 46 circuits, main circuit main
module main (
  input  in_1,
  input  [15:0] RAM_Input,
  input  RAM_IN_SET,
  input  [15:0] RAM_Address_IN
);

  wire alu_final_1_carry_out_flag, alu_final_1_equal_flag, alu_final_1_greaterthan_flag,
       alu_final_1_lessthan_flag, alu_final_1_overflow_flag, alu_final_1_undefined_status_flag,
       alu_final_1_underflow_flag, alu_final_1_zero_flag, clock_1_out, control_unit_beginning_1_acc_enable,
       control_unit_beginning_1_acc_set, control_unit_beginning_1_bus_1, control_unit_beginning_1_flag_set,
       control_unit_beginning_1_iar_enable, control_unit_beginning_1_iar_set,
       control_unit_beginning_1_ir_set, control_unit_beginning_1_r1, control_unit_beginning_1_r1_set,
       control_unit_beginning_1_r2, control_unit_beginning_1_r2_set, control_unit_beginning_1_r3,
       control_unit_beginning_1_r3_set, control_unit_beginning_1_r4, control_unit_beginning_1_r4_set,
       control_unit_beginning_1_ram_enable, control_unit_beginning_1_ram_set,
       control_unit_beginning_1_tmp_set, flag_register_1_carry, flag_register_1_equal,
       flag_register_1_greater, flag_register_1_less, flag_register_1_overflow, flag_register_1_undefined,
       flag_register_1_underflow, flag_register_1_zero, LOAD;
  wire [3:0] control_unit_beginning_1_opcode_to_alu;
  wire [15:0] alu_final_1_output_of_operation_xxxx, bus_1_circuit_1_out_pins, multiplexer_1_out,
       tmp_circuit_1_tmp_o, undriven;

  TMP_Circuit tmp_circuit_1 (
    .TMP_i(RAM_Address_IN), .TMP_SET(control_unit_beginning_1_tmp_set), .TMP_o(tmp_circuit_1_tmp_o));
  BUS_1_CIRCUIT bus_1_circuit_1 (
    .in_pins(tmp_circuit_1_tmp_o), .BUS_1V(control_unit_beginning_1_bus_1),
    .out_pins(bus_1_circuit_1_out_pins));
  ALU_final alu_final_1 (
    .a(RAM_Address_IN), .b(bus_1_circuit_1_out_pins), .opcode(control_unit_beginning_1_opcode_to_alu),
    .output_of_operation_xxxx(alu_final_1_output_of_operation_xxxx),
    .GreaterThan_FLAG(alu_final_1_greaterthan_flag), .EQUAL_FLAG(alu_final_1_equal_flag),
    .LessThan_FLAG(alu_final_1_lessthan_flag), .undefined_status_flag(alu_final_1_undefined_status_flag),
    .CARRY_OUT_FLAG(alu_final_1_carry_out_flag), .ZERO_FLAG(alu_final_1_zero_flag),
    .overflow_flag(alu_final_1_overflow_flag), .underflow_flag(alu_final_1_underflow_flag));
  ACC_Circuit acc_circuit_1 (
    .ACC_INPUT(alu_final_1_output_of_operation_xxxx), .ACC_SET(control_unit_beginning_1_acc_set),
    .ACC_ENABLE(control_unit_beginning_1_acc_enable), .ACC_OUTPUT(RAM_Address_IN));
  FLAG_Register flag_register_1 (
    .Carry_FLAG(alu_final_1_carry_out_flag), .Greater_Than_FLAG(alu_final_1_greaterthan_flag),
    .Equal_FLAG(alu_final_1_equal_flag), .Zero_FLAG(alu_final_1_zero_flag),
    .Undefined_FLAG(alu_final_1_undefined_status_flag), .Overflow_FLAG(alu_final_1_overflow_flag),
    .Underflow_FLAG(alu_final_1_underflow_flag), .Less_Than_FLAG(alu_final_1_lessthan_flag),
    .FLAG_SET(control_unit_beginning_1_flag_set), .Carry(flag_register_1_carry),
    .Greater(flag_register_1_greater), .Equal(flag_register_1_equal), .Zero(flag_register_1_zero),
    .Undefined(flag_register_1_undefined), .Overflow(flag_register_1_overflow),
    .Underflow(flag_register_1_underflow), .Less(flag_register_1_less));
  GENERAL_PURPOSE_REGISTERS_Rx general_purpose_registers_rx_1 (
    .Rx_INPUT(RAM_Address_IN), .Rx_SET(control_unit_beginning_1_r1_set),
    .Rx_ENABLE(control_unit_beginning_1_r1), .Rx_OUTPUT(RAM_Address_IN));
  Clock clock_1 (.out(clock_1_out));
  GENERAL_PURPOSE_REGISTERS_Rx general_purpose_registers_rx_2 (
    .Rx_INPUT(RAM_Address_IN), .Rx_SET(control_unit_beginning_1_r2_set),
    .Rx_ENABLE(control_unit_beginning_1_r2), .Rx_OUTPUT(RAM_Address_IN));
  IAR_Circuit iar_circuit_1 (
    .IAR_INPUT(RAM_Address_IN), .IAR_SET(control_unit_beginning_1_iar_set),
    .IAR_ENABLE(control_unit_beginning_1_iar_enable), .IAR_OUTPUT(RAM_Address_IN));
  CONTROL_UNIT_BEGINNING control_unit_beginning_1 (
    .CLK_INPUT(clock_1_out), .IR(undriven), .Carry_FLAG(flag_register_1_carry),
    .Greater_Than_Flag(flag_register_1_greater), .Equal_Flag(flag_register_1_equal),
    .Zero_Flag(flag_register_1_zero), .Undefined_Flag(flag_register_1_undefined),
    .Overflow_Flag(flag_register_1_overflow), .Underflow_Flag(flag_register_1_underflow),
    .Less_Than_Flag(flag_register_1_less), .stepper_reset(in_1), .R1_SET(control_unit_beginning_1_r1_set),
    .R1(control_unit_beginning_1_r1), .R2_SET(control_unit_beginning_1_r2_set),
    .R2(control_unit_beginning_1_r2), .R3_SET(control_unit_beginning_1_r3_set),
    .R3(control_unit_beginning_1_r3), .R4_SET(control_unit_beginning_1_r4_set),
    .R4(control_unit_beginning_1_r4), .TMP_SET(control_unit_beginning_1_tmp_set),
    .ACC_SET(control_unit_beginning_1_acc_set), .MAR_SET(RAM_IN_SET),
    .ACC_ENABLE(control_unit_beginning_1_acc_enable), .RAM_SET(control_unit_beginning_1_ram_set),
    .opcode_to_alu(control_unit_beginning_1_opcode_to_alu), .IR_SET(control_unit_beginning_1_ir_set),
    .RAM_ENABLE(control_unit_beginning_1_ram_enable), .IAR_SET(control_unit_beginning_1_iar_set),
    .IAR_ENABLE(control_unit_beginning_1_iar_enable), .BUS_1(control_unit_beginning_1_bus_1),
    .FLAG_SET(control_unit_beginning_1_flag_set));
  GENERAL_PURPOSE_REGISTERS_Rx general_purpose_registers_rx_3 (
    .Rx_INPUT(RAM_Address_IN), .Rx_SET(control_unit_beginning_1_r3_set),
    .Rx_ENABLE(control_unit_beginning_1_r3), .Rx_OUTPUT(RAM_Address_IN));
  IR_Circuit ir_circuit_1 (.IR_INPUT(undriven), .IR_SET(control_unit_beginning_1_ir_set), .IR_OUTPUT(RAM_Address_IN));
  GENERAL_PURPOSE_REGISTERS_Rx general_purpose_registers_rx_4 (
    .Rx_INPUT(RAM_Address_IN), .Rx_SET(control_unit_beginning_1_r4_set),
    .Rx_ENABLE(control_unit_beginning_1_r4), .Rx_OUTPUT(RAM_Address_IN));
  Multiplexer #(.width(16)) multiplexer_1 (.in0(RAM_Address_IN), .in1(RAM_Input), .out(multiplexer_1_out), .sel(LOAD));
  RAM_128K ram_128k_1 (
    .MAR_IN(RAM_Address_IN), .MAR_SET(RAM_IN_SET), .write_enable(control_unit_beginning_1_ram_set),
    .allow_output(control_unit_beginning_1_ram_enable), .input_value(multiplexer_1_out),
    .output_value(RAM_Address_IN));
endmodule

module AND_16_Bit (
  input  [15:0] A,
  input  [15:0] B,
  output [15:0] O
);

  and and_1 (O[15], A[15], B[15]);
  and and_2 (O[14], A[14], B[14]);
  and and_3 (O[13], A[13], B[13]);
  and and_4 (O[12], A[12], B[12]);
  and and_5 (O[11], A[11], B[11]);
  and and_6 (O[10], A[10], B[10]);
  and and_7 (O[9], A[9], B[9]);
  and and_8 (O[8], A[8], B[8]);
  and and_9 (O[7], A[7], B[7]);
  and and_10 (O[6], A[6], B[6]);
  and and_11 (O[5], A[5], B[5]);
  and and_12 (O[4], A[4], B[4]);
  and and_13 (O[3], A[3], B[3]);
  and and_14 (O[2], A[2], B[2]);
  and and_15 (O[1], A[1], B[1]);
  and and_16 (O[0], A[0], B[0]);
endmodule

module OR_16_BIT (
  input  [15:0] A,
  input  [15:0] B,
  output [15:0] O
);

  assign O = A | B;  // OR_Gate or_1, 16 bits wide
endmodule

module X0R_16_BIT (
  input  [15:0] A,
  input  [15:0] B,
  output [15:0] O
);

  assign O = A ^ B;  // XOR_Gate xor_1, 16 bits wide
endmodule

module MEMORY_1_BIT (
  input  S,
  output Q
);

  wire nand_1_out, nand_2_out, nand_4_out, not_1_out;

  not not_1 (not_1_out, S);
  nand nand_1 (nand_1_out, 1'b1, not_1_out);
  nand nand_2 (nand_2_out, S, 1'b1);
  nand nand_3 (Q, nand_2_out, nand_4_out);
  nand nand_4 (nand_4_out, Q, nand_1_out);
endmodule

module MEMORY_8_BIT (
  input  [7:0] in_1,
  output [7:0] Q
);

  MEMORY_1_BIT memory_1_bit_1 (.S(in_1[0]), .Q(Q[0]));
  MEMORY_1_BIT memory_1_bit_2 (.S(in_1[1]), .Q(Q[1]));
  MEMORY_1_BIT memory_1_bit_3 (.S(in_1[3]), .Q(Q[3]));
  MEMORY_1_BIT memory_1_bit_4 (.S(in_1[4]), .Q(Q[4]));
  MEMORY_1_BIT memory_1_bit_5 (.S(in_1[5]), .Q(Q[5]));
  MEMORY_1_BIT memory_1_bit_6 (.S(in_1[6]), .Q(Q[6]));
  MEMORY_1_BIT memory_1_bit_7 (.S(in_1[7]), .Q(Q[7]));
  MEMORY_1_BIT memory_1_bit_8 (.S(in_1[2]), .Q(Q[2]));
endmodule

module MEMORY_16_BIT (
  input  [15:0] in_1,
  output [15:0] Q
);

  MEMORY_8_BIT memory_8_bit_1 (.in_1(in_1[7:0]), .Q(Q[7:0]));
  MEMORY_8_BIT memory_8_bit_2 (.in_1(in_1[15:8]), .Q(Q[15:8]));

  // Notes on the sheet:
  //   s
  //   e
  //   s
  //   e
  //   Q
  //   Q
endmodule

module SHIFT_LEFT (
  input  [15:0] Inputs,
  output [15:0] Outputs,
  output Overflow
);

  MEMORY_16_BIT memory_16_bit_1 (.in_1(Inputs), .Q({Overflow, Outputs[15:1]}));

  assign Outputs[0] = 1'b0;

  // Notes on the sheet:
  //   s
  //   e
  //   Q
endmodule

module SHIFT_RIGHT (
  input  [15:0] Inputs,
  output Underflow,
  output [15:0] Outputs
);

  MEMORY_16_BIT memory_16_bit_1 (.in_1(Inputs), .Q({Outputs[14:0], Underflow}));

  assign Outputs[15] = 1'b0;

  // Notes on the sheet:
  //   s
  //   e
  //   Q
endmodule

module CIRCULAR_LEFT_SHIFT (
  input  [15:0] Inputs,
  output [15:0] Outputs
);

  MEMORY_16_BIT memory_16_bit_1 (.in_1(Inputs), .Q({Outputs[0], Outputs[15:1]}));

  // Notes on the sheet:
  //   s
  //   e
  //   Q
endmodule

module CIRCULAR_RIGHT_SHIFT (
  input  [15:0] Inputs,
  output [15:0] Outputus
);

  MEMORY_16_BIT memory_16_bit_1 (.in_1(Inputs), .Q({Outputus[14:0], Outputus[15]}));

  // Notes on the sheet:
  //   s
  //   e
  //   Q
endmodule

module DIVISION_16_BIT (
  input  [15:0] a,
  input  [15:0] b,
  output [15:0] quotient_output,
  output carry_undefined
);

  wire or_1_out;
  wire [15:0] divider_1_out;

  Divider #(.width(16)) divider_1 (.a(a), .b(b), .out(divider_1_out));  // open: upper, rem
  or or_1 (or_1_out, b[0], b[1], b[2], b[3], b[4], b[5], b[6], b[7], b[8], b[9], b[10], b[11], b[12], b[13], b[14], b[15]);
  and and_1 (quotient_output[0], divider_1_out[0], or_1_out);
  and and_2 (quotient_output[1], divider_1_out[1], or_1_out);
  and and_3 (quotient_output[2], divider_1_out[2], or_1_out);
  and and_4 (quotient_output[3], divider_1_out[3], or_1_out);
  and and_5 (quotient_output[4], divider_1_out[4], or_1_out);
  and and_6 (quotient_output[5], divider_1_out[5], or_1_out);
  and and_7 (quotient_output[6], divider_1_out[6], or_1_out);
  and and_8 (quotient_output[7], divider_1_out[7], or_1_out);
  and and_9 (quotient_output[8], divider_1_out[8], or_1_out);
  and and_10 (quotient_output[9], divider_1_out[9], or_1_out);
  and and_11 (quotient_output[10], divider_1_out[10], or_1_out);
  and and_12 (quotient_output[11], divider_1_out[11], or_1_out);
  and and_13 (quotient_output[12], divider_1_out[12], or_1_out);
  and and_14 (quotient_output[13], divider_1_out[13], or_1_out);
  and and_15 (quotient_output[14], divider_1_out[14], or_1_out);
  and and_16 (quotient_output[15], or_1_out, divider_1_out[15]);
  not not_1 (carry_undefined, or_1_out);
endmodule

module MODULO_16_BIT (
  input  [15:0] a,
  input  [15:0] b,
  output [15:0] modulo_output
);

  Divider #(.width(16)) divider_1 (.a(a), .b(b), .rem(modulo_output));  // open: out, upper
endmodule

module INCREMENT_16_BIT (
  input  [15:0] a,
  output [15:0] output_inc,
  output carry_inc
);

  Adder #(.width(16)) adder_1 (.a(a), .b(16'h1), .out(output_inc), .cout(carry_inc));  // open: cin
endmodule

module DECREMENT_16_BIT (
  input  [15:0] a,
  output [15:0] output_decrement,
  output carry_dec
);

  Subtractor #(.width(16)) subtractor_1 (.a(a), .b(16'h1), .out(output_decrement), .bout(carry_dec));  // open: bin
endmodule

module MULTIPLICATION_16_BIT (
  input  [15:0] a,
  input  [15:0] b,
  output [15:0] output_mul,
  output invalid_flag
);

  wire or_1_out, or_2_out;

  Multiplier multiplier_1 (.a(a[7:0]), .b(b[7:0]), .out(output_mul[7:0]), .cout(output_mul[15:8]));  // open: cin
  or or_1 (or_1_out, a[8], a[9], a[10], a[11], a[12], a[13], a[14], a[15]);
  or or_2 (or_2_out, b[15], b[14], b[13], b[12], b[11], b[10], b[9], b[8]);
  or or_3 (invalid_flag, or_2_out, or_1_out);
endmodule

module FULL_ADDER_16_BIT (
  input  [15:0] A,
  input  [15:0] B,
  input  Cin,
  output [15:0] S,
  output Cout
);

  wire adder_1_bit_1_cout, adder_1_bit_2_cout, adder_1_bit_3_cout, adder_1_bit_4_cout, adder_1_bit_5_cout,
       adder_1_bit_6_cout, adder_1_bit_7_cout, adder_1_bit_8_cout, adder_1_bit_9_cout, adder_1_bit_10_cout,
       adder_1_bit_11_cout, adder_1_bit_12_cout, adder_1_bit_13_cout, adder_1_bit_14_cout,
       adder_1_bit_15_cout, undriven;

  ADDER_1_BIT adder_1_bit_1 (.Cin(undriven), .A(A[0]), .B(B[0]), .Sum(S[0]), .Cout(adder_1_bit_1_cout));
  ADDER_1_BIT adder_1_bit_2 (.Cin(adder_1_bit_1_cout), .A(A[1]), .B(B[1]), .Sum(S[1]), .Cout(adder_1_bit_2_cout));
  ADDER_1_BIT adder_1_bit_3 (.Cin(adder_1_bit_2_cout), .A(A[2]), .B(B[2]), .Sum(S[2]), .Cout(adder_1_bit_3_cout));
  ADDER_1_BIT adder_1_bit_4 (.Cin(adder_1_bit_3_cout), .A(A[3]), .B(B[3]), .Sum(S[3]), .Cout(adder_1_bit_4_cout));
  ADDER_1_BIT adder_1_bit_5 (.Cin(adder_1_bit_4_cout), .A(A[4]), .B(B[4]), .Sum(S[4]), .Cout(adder_1_bit_5_cout));
  ADDER_1_BIT adder_1_bit_6 (.Cin(adder_1_bit_5_cout), .A(A[5]), .B(B[5]), .Sum(S[5]), .Cout(adder_1_bit_6_cout));
  ADDER_1_BIT adder_1_bit_7 (.Cin(adder_1_bit_6_cout), .A(A[6]), .B(B[6]), .Sum(S[6]), .Cout(adder_1_bit_7_cout));
  ADDER_1_BIT adder_1_bit_8 (.Cin(adder_1_bit_7_cout), .A(A[7]), .B(B[7]), .Sum(S[7]), .Cout(adder_1_bit_8_cout));
  ADDER_1_BIT adder_1_bit_9 (.Cin(adder_1_bit_8_cout), .A(A[8]), .B(B[8]), .Sum(S[8]), .Cout(adder_1_bit_9_cout));
  ADDER_1_BIT adder_1_bit_10 (.Cin(adder_1_bit_9_cout), .A(A[9]), .B(B[9]), .Sum(S[9]), .Cout(adder_1_bit_10_cout));
  ADDER_1_BIT adder_1_bit_11 (.Cin(adder_1_bit_10_cout), .A(A[10]), .B(B[10]), .Sum(S[10]), .Cout(adder_1_bit_11_cout));
  ADDER_1_BIT adder_1_bit_12 (.Cin(adder_1_bit_11_cout), .A(A[11]), .B(B[11]), .Sum(S[11]), .Cout(adder_1_bit_12_cout));
  ADDER_1_BIT adder_1_bit_13 (.Cin(adder_1_bit_12_cout), .A(A[12]), .B(B[12]), .Sum(S[12]), .Cout(adder_1_bit_13_cout));
  ADDER_1_BIT adder_1_bit_14 (.Cin(adder_1_bit_13_cout), .A(A[13]), .B(B[13]), .Sum(S[13]), .Cout(adder_1_bit_14_cout));
  ADDER_1_BIT adder_1_bit_15 (.Cin(adder_1_bit_14_cout), .A(A[14]), .B(B[14]), .Sum(S[14]), .Cout(adder_1_bit_15_cout));
  ADDER_1_BIT adder_1_bit_16 (.Cin(adder_1_bit_15_cout), .A(A[15]), .B(B[15]), .Sum(S[15]), .Cout(Cout));
endmodule

module ADDER_1_BIT (
  input  Cin,
  input  A,
  input  B,
  output Sum,
  output Cout
);

  wire and_1_out, and_2_out, xor_1_out;

  xor xor_1 (xor_1_out, A, B);
  and and_1 (and_1_out, xor_1_out, Cin);
  and and_2 (and_2_out, A, B);
  xor xor_2 (Sum, Cin, xor_1_out);
  or or_1 (Cout, and_1_out, and_2_out);
endmodule

module ADD_WITHOUT_CARRY_16_BITS (
  input  [15:0] A,
  input  [15:0] B,
  output [15:0] S,
  output Cout
);

  wire adder_1_bit_1_cout, adder_1_bit_2_cout, adder_1_bit_3_cout, adder_1_bit_4_cout, adder_1_bit_5_cout,
       adder_1_bit_6_cout, adder_1_bit_7_cout, adder_1_bit_8_cout, adder_1_bit_9_cout, adder_1_bit_10_cout,
       adder_1_bit_11_cout, adder_1_bit_12_cout, adder_1_bit_13_cout, adder_1_bit_14_cout,
       adder_1_bit_15_cout;

  ADDER_1_BIT adder_1_bit_1 (.Cin(1'b0), .A(A[0]), .B(B[0]), .Sum(S[0]), .Cout(adder_1_bit_1_cout));
  ADDER_1_BIT adder_1_bit_2 (.Cin(adder_1_bit_1_cout), .A(A[1]), .B(B[1]), .Sum(S[1]), .Cout(adder_1_bit_2_cout));
  ADDER_1_BIT adder_1_bit_3 (.Cin(adder_1_bit_2_cout), .A(A[2]), .B(B[2]), .Sum(S[2]), .Cout(adder_1_bit_3_cout));
  ADDER_1_BIT adder_1_bit_4 (.Cin(adder_1_bit_3_cout), .A(A[3]), .B(B[3]), .Sum(S[3]), .Cout(adder_1_bit_4_cout));
  ADDER_1_BIT adder_1_bit_5 (.Cin(adder_1_bit_4_cout), .A(A[4]), .B(B[4]), .Sum(S[4]), .Cout(adder_1_bit_5_cout));
  ADDER_1_BIT adder_1_bit_6 (.Cin(adder_1_bit_5_cout), .A(A[5]), .B(B[5]), .Sum(S[5]), .Cout(adder_1_bit_6_cout));
  ADDER_1_BIT adder_1_bit_7 (.Cin(adder_1_bit_6_cout), .A(A[6]), .B(B[6]), .Sum(S[6]), .Cout(adder_1_bit_7_cout));
  ADDER_1_BIT adder_1_bit_8 (.Cin(adder_1_bit_7_cout), .A(A[7]), .B(B[7]), .Sum(S[7]), .Cout(adder_1_bit_8_cout));
  ADDER_1_BIT adder_1_bit_9 (.Cin(adder_1_bit_8_cout), .A(A[8]), .B(B[8]), .Sum(S[8]), .Cout(adder_1_bit_9_cout));
  ADDER_1_BIT adder_1_bit_10 (.Cin(adder_1_bit_9_cout), .A(A[9]), .B(B[9]), .Sum(S[9]), .Cout(adder_1_bit_10_cout));
  ADDER_1_BIT adder_1_bit_11 (.Cin(adder_1_bit_10_cout), .A(A[10]), .B(B[10]), .Sum(S[10]), .Cout(adder_1_bit_11_cout));
  ADDER_1_BIT adder_1_bit_12 (.Cin(adder_1_bit_11_cout), .A(A[11]), .B(B[11]), .Sum(S[11]), .Cout(adder_1_bit_12_cout));
  ADDER_1_BIT adder_1_bit_13 (.Cin(adder_1_bit_12_cout), .A(A[12]), .B(B[12]), .Sum(S[12]), .Cout(adder_1_bit_13_cout));
  ADDER_1_BIT adder_1_bit_14 (.Cin(adder_1_bit_13_cout), .A(A[13]), .B(B[13]), .Sum(S[13]), .Cout(adder_1_bit_14_cout));
  ADDER_1_BIT adder_1_bit_15 (.Cin(adder_1_bit_14_cout), .A(A[14]), .B(B[14]), .Sum(S[14]), .Cout(adder_1_bit_15_cout));
  ADDER_1_BIT adder_1_bit_16 (.Cin(adder_1_bit_15_cout), .A(A[15]), .B(B[15]), .Sum(S[15]), .Cout(Cout));
endmodule

module ALU_final (
  input  [15:0] a,
  input  [15:0] b,
  input  [3:0] opcode,
  output [15:0] output_of_operation_xxxx,
  output GreaterThan_FLAG,
  output EQUAL_FLAG,
  output LessThan_FLAG,
  output undefined_status_flag,
  output CARRY_OUT_FLAG,
  output ZERO_FLAG,
  output overflow_flag,
  output underflow_flag
);

  wire add_without_carry_16_bits_1_cout, decrement_16_bit_1_carry_dec, division_16_bit_1_carry_undefined,
       full_adder_16_bit_1_cout, increment_16_bit_1_carry_inc, multiplication_16_bit_1_invalid_flag,
       or_1_out, shift_left_1_overflow, shift_right_1_underflow, subtractor_16bit_1_bout,
       subtractor_16bit_1_negative_overflow, subtractor_without_borrow_1_bout,
       subtractor_without_borrow_1_negative_overflow;
  wire [15:0] add_without_carry_16_bits_1_s, and_16_bit_1_o, circular_left_shift_1_outputs,
       circular_right_shift_1_outputus, decrement_16_bit_1_output_decrement,
       division_16_bit_1_quotient_output, full_adder_16_bit_1_s, increment_16_bit_1_output_inc,
       modulo_16_bit_1_modulo_output, multiplication_16_bit_1_output_mul, or_16_bit_1_o,
       shift_left_1_outputs, shift_right_1_outputs, subtractor_16bit_1_difference,
       subtractor_without_borrow_1_difference, x0r_16_bit_1_o;

  Comparator #(.mode("unsigned"), .width(16)) comparator_1 (
    .a(a), .b(b), .gt(GreaterThan_FLAG), .eq(EQUAL_FLAG), .lt(LessThan_FLAG));
  SUBTRACTOR_WITHOUT_BORROW subtractor_without_borrow_1 (
    .B(b), .A(a), .Difference(subtractor_without_borrow_1_difference),
    .negative_overflow(subtractor_without_borrow_1_negative_overflow), .Bout(subtractor_without_borrow_1_bout));
  AND_16_Bit and_16_bit_1 (.A(a), .B(b), .O(and_16_bit_1_o));
  OR_16_BIT or_16_bit_1 (.A(a), .B(b), .O(or_16_bit_1_o));
  X0R_16_BIT x0r_16_bit_1 (.A(a), .B(b), .O(x0r_16_bit_1_o));
  SHIFT_LEFT shift_left_1 (.Inputs(a), .Outputs(shift_left_1_outputs), .Overflow(shift_left_1_overflow));
  SHIFT_RIGHT shift_right_1 (.Inputs(a), .Underflow(shift_right_1_underflow), .Outputs(shift_right_1_outputs));
  CIRCULAR_LEFT_SHIFT circular_left_shift_1 (.Inputs(a), .Outputs(circular_left_shift_1_outputs));
  CIRCULAR_RIGHT_SHIFT circular_right_shift_1 (.Inputs(a), .Outputus(circular_right_shift_1_outputus));
  DIVISION_16_BIT division_16_bit_1 (
    .a(a), .b(b), .quotient_output(division_16_bit_1_quotient_output),
    .carry_undefined(division_16_bit_1_carry_undefined));
  MODULO_16_BIT modulo_16_bit_1 (.a(a), .b(b), .modulo_output(modulo_16_bit_1_modulo_output));
  INCREMENT_16_BIT increment_16_bit_1 (
    .a(a), .output_inc(increment_16_bit_1_output_inc), .carry_inc(increment_16_bit_1_carry_inc));
  DECREMENT_16_BIT decrement_16_bit_1 (
    .a(a), .output_decrement(decrement_16_bit_1_output_decrement), .carry_dec(decrement_16_bit_1_carry_dec));
  MULTIPLICATION_16_BIT multiplication_16_bit_1 (
    .a(a), .b(b), .output_mul(multiplication_16_bit_1_output_mul),
    .invalid_flag(multiplication_16_bit_1_invalid_flag));
  FULL_ADDER_16_BIT full_adder_16_bit_1 (
    .A(a), .B(b), .Cin(1'b1), .S(full_adder_16_bit_1_s), .Cout(full_adder_16_bit_1_cout));
  ADD_WITHOUT_CARRY_16_BITS add_without_carry_16_bits_1 (
    .A(a), .B(b), .S(add_without_carry_16_bits_1_s), .Cout(add_without_carry_16_bits_1_cout));
  SUBTRACTOR_16BIT subtractor_16bit_1 (
    .B(b), .A(a), .Bin(1'b1), .Difference(subtractor_16bit_1_difference),
    .negative_overflow(subtractor_16bit_1_negative_overflow), .Bout(subtractor_16bit_1_bout));
  Multiplexer #(.select(4), .width(16)) multiplexer_1 (
    .in0(add_without_carry_16_bits_1_s), .in1(or_16_bit_1_o), .in2(x0r_16_bit_1_o),
    .in3(shift_left_1_outputs), .in4(shift_right_1_outputs), .in5(circular_left_shift_1_outputs),
    .in6(circular_right_shift_1_outputus), .in7(division_16_bit_1_quotient_output),
    .in8(modulo_16_bit_1_modulo_output), .in9(increment_16_bit_1_output_inc),
    .in10(decrement_16_bit_1_output_decrement), .in11(multiplication_16_bit_1_output_mul),
    .in12(full_adder_16_bit_1_s), .in13(and_16_bit_1_o), .in14(subtractor_16bit_1_difference),
    .in15(subtractor_without_borrow_1_difference), .out(output_of_operation_xxxx), .sel(opcode));
  Multiplexer #(.select(4)) multiplexer_2 (
    .in0(add_without_carry_16_bits_1_cout), .in3(shift_left_1_overflow), .in9(increment_16_bit_1_carry_inc),
    .in10(decrement_16_bit_1_carry_dec), .in11(multiplication_16_bit_1_invalid_flag),
    .in12(full_adder_16_bit_1_cout), .out(overflow_flag), .sel(opcode));  // open: in1, in2, in4, in5, in6, in7, in8, in13, in14, in15
  Multiplexer #(.select(4)) multiplexer_3 (
    .in4(shift_right_1_underflow), .in14(subtractor_16bit_1_negative_overflow),
    .in15(subtractor_without_borrow_1_negative_overflow), .out(underflow_flag), .sel(opcode));  // open: in0, in1, in2, in3, in5, in6, in7, in8, in9, in10, in11, in12, in13
  Multiplexer #(.select(4)) multiplexer_4 (
    .in7(division_16_bit_1_carry_undefined), .out(undefined_status_flag), .sel(opcode));  // open: in0, in1, in2, in3, in4, in5, in6, in8, in9, in10, in11, in12, in13, in14, in15
  Multiplexer #(.select(4)) multiplexer_5 (
    .in0(add_without_carry_16_bits_1_cout), .out(CARRY_OUT_FLAG), .sel(opcode));  // open: in1, in2, in3, in4, in5, in6, in7, in8, in9, in10, in11, in12, in13, in14, in15
  or or_1 (or_1_out, output_of_operation_xxxx[15], output_of_operation_xxxx[14], output_of_operation_xxxx[13], output_of_operation_xxxx[12], output_of_operation_xxxx[11], output_of_operation_xxxx[10], output_of_operation_xxxx[9], output_of_operation_xxxx[8], output_of_operation_xxxx[6], output_of_operation_xxxx[5], output_of_operation_xxxx[4], output_of_operation_xxxx[3], output_of_operation_xxxx[2], output_of_operation_xxxx[1], output_of_operation_xxxx[0], output_of_operation_xxxx[7]);
  not not_1 (ZERO_FLAG, or_1_out);
  // also tied to GND on the sheet: {subtractor_without_borrow_1_bout, subtractor_16bit_1_bout}

  // Notes on the sheet:
  //   a: pull=down
  //   Arithmetic and Logic Unit of our Microprocessor
endmodule

module ALU_testing (
  input  in_1,
  input  [15:0] in_2,
  input  [15:0] in_3,
  input  [3:0] in_4,
  output [15:0] out_5,
  output out_6,
  output out_7,
  output out_8,
  output out_9
);

  wire alu_final_1_p5;

  // ALU_final alu_final_1: pin names not known; wires that end beside it: in_2, in_3, in_1, in_4, alu_final_1_p5, out_5, out_6, out_7, out_8, out_9

  // Notes on the sheet:
  //   OP-CODE
  //   0000
  //   0001
  //   0010
  //   0011
  //   0100
  //   0101
  //   0110
  //   0111
  //   1000
  //   1001
  //   1010
  //   1011
  //   1100
  //   1101
  //   1110
  //   1111
  //   Register File
  //   INSTRUCTION
  //   OR OPERATION
  //   ADD OPERATION
  //   XOR OPERATION
  //   SHIFT LEFT OPERATION
  //   SHIFT RIGHT OPERATION
  //   CIRCULAR LEFT SHIFT OPERATION
  //   CIRCULAR RIGHT SHIFT OPERATION
  //   DIVISION OPERATION
  //   MODULO OPERATION
  //   INCREMENT OPERATION
  //   DECREMENT OPERATION
  //   MULTIPLICATION OPERATION
  //   ADD WITH CARRY-IN
  //   AND OPERATION
  //   SUBTRACT WITH BORROW-IN
  //   SUBTRACT OPERATION
  //   Multiplication is 8 bit by 8 bit multiplication. So, your multiplication should be 00000000xxxxxxxx times 00000000xxxxxxxx
endmodule

module SUBTRACTOR_1BIT (
  input  A,
  input  B,
  input  Bin,
  output D,
  output Bout
);

  wire and_1_out, and_2_out, and_3_out, not_1_out, xor_1_out;

  not not_1 (not_1_out, A);
  and and_1 (and_1_out, not_1_out, B);
  and and_2 (and_2_out, B, Bin);
  and and_3 (and_3_out, not_1_out, Bin);
  xor xor_1 (xor_1_out, A, B);
  xor xor_2 (D, xor_1_out, Bin);
  or or_1 (Bout, and_1_out, and_3_out, and_2_out);
endmodule

module SUBTRACTOR_16BIT (
  input  [15:0] B,
  input  [15:0] A,
  input  Bin,
  output [15:0] Difference,
  output negative_overflow,
  output Bout
);

  wire comparator_1_lt, not_1_out, subtractor_1bit_1_bout, subtractor_1bit_1_d, subtractor_1bit_2_bout,
       subtractor_1bit_2_d, subtractor_1bit_3_bout, subtractor_1bit_3_d, subtractor_1bit_4_bout,
       subtractor_1bit_4_d, subtractor_1bit_5_bout, subtractor_1bit_5_d, subtractor_1bit_6_bout,
       subtractor_1bit_6_d, subtractor_1bit_7_bout, subtractor_1bit_7_d, subtractor_1bit_8_bout,
       subtractor_1bit_8_d, subtractor_1bit_9_bout, subtractor_1bit_9_d, subtractor_1bit_10_bout,
       subtractor_1bit_10_d, subtractor_1bit_11_bout, subtractor_1bit_11_d, subtractor_1bit_12_bout,
       subtractor_1bit_12_d, subtractor_1bit_13_bout, subtractor_1bit_13_d, subtractor_1bit_14_bout,
       subtractor_1bit_14_d, subtractor_1bit_15_bout, subtractor_1bit_15_d, subtractor_1bit_16_d;

  Comparator #(.mode("unsigned"), .width(16)) comparator_1 (.a(A), .b(B), .lt(comparator_1_lt));  // open: gt, eq
  not not_1 (not_1_out, comparator_1_lt);
  SUBTRACTOR_1BIT subtractor_1bit_1 (
    .A(A[0]), .B(B[0]), .Bin(Bin), .D(subtractor_1bit_1_d), .Bout(subtractor_1bit_1_bout));
  SUBTRACTOR_1BIT subtractor_1bit_2 (
    .A(A[1]), .B(B[1]), .Bin(subtractor_1bit_1_bout), .D(subtractor_1bit_2_d), .Bout(subtractor_1bit_2_bout));
  SUBTRACTOR_1BIT subtractor_1bit_3 (
    .A(A[2]), .B(B[2]), .Bin(subtractor_1bit_2_bout), .D(subtractor_1bit_3_d), .Bout(subtractor_1bit_3_bout));
  SUBTRACTOR_1BIT subtractor_1bit_4 (
    .A(A[3]), .B(B[3]), .Bin(subtractor_1bit_3_bout), .D(subtractor_1bit_4_d), .Bout(subtractor_1bit_4_bout));
  SUBTRACTOR_1BIT subtractor_1bit_5 (
    .A(A[4]), .B(B[4]), .Bin(subtractor_1bit_4_bout), .D(subtractor_1bit_5_d), .Bout(subtractor_1bit_5_bout));
  SUBTRACTOR_1BIT subtractor_1bit_6 (
    .A(A[5]), .B(B[5]), .Bin(subtractor_1bit_5_bout), .D(subtractor_1bit_6_d), .Bout(subtractor_1bit_6_bout));
  SUBTRACTOR_1BIT subtractor_1bit_7 (
    .A(A[6]), .B(B[6]), .Bin(subtractor_1bit_6_bout), .D(subtractor_1bit_7_d), .Bout(subtractor_1bit_7_bout));
  SUBTRACTOR_1BIT subtractor_1bit_8 (
    .A(A[7]), .B(B[7]), .Bin(subtractor_1bit_7_bout), .D(subtractor_1bit_8_d), .Bout(subtractor_1bit_8_bout));
  SUBTRACTOR_1BIT subtractor_1bit_9 (
    .A(A[8]), .B(B[8]), .Bin(subtractor_1bit_8_bout), .D(subtractor_1bit_9_d), .Bout(subtractor_1bit_9_bout));
  SUBTRACTOR_1BIT subtractor_1bit_10 (
    .A(A[9]), .B(B[9]), .Bin(subtractor_1bit_9_bout), .D(subtractor_1bit_10_d), .Bout(subtractor_1bit_10_bout));
  SUBTRACTOR_1BIT subtractor_1bit_11 (
    .A(A[10]), .B(B[10]), .Bin(subtractor_1bit_10_bout), .D(subtractor_1bit_11_d),
    .Bout(subtractor_1bit_11_bout));
  SUBTRACTOR_1BIT subtractor_1bit_12 (
    .A(A[11]), .B(B[11]), .Bin(subtractor_1bit_11_bout), .D(subtractor_1bit_12_d),
    .Bout(subtractor_1bit_12_bout));
  SUBTRACTOR_1BIT subtractor_1bit_13 (
    .A(A[12]), .B(B[12]), .Bin(subtractor_1bit_12_bout), .D(subtractor_1bit_13_d),
    .Bout(subtractor_1bit_13_bout));
  SUBTRACTOR_1BIT subtractor_1bit_14 (
    .A(A[13]), .B(B[13]), .Bin(subtractor_1bit_13_bout), .D(subtractor_1bit_14_d),
    .Bout(subtractor_1bit_14_bout));
  SUBTRACTOR_1BIT subtractor_1bit_15 (
    .A(A[14]), .B(B[14]), .Bin(subtractor_1bit_14_bout), .D(subtractor_1bit_15_d),
    .Bout(subtractor_1bit_15_bout));
  SUBTRACTOR_1BIT subtractor_1bit_16 (
    .A(A[15]), .B(B[15]), .Bin(subtractor_1bit_15_bout), .D(subtractor_1bit_16_d), .Bout(Bout));
  not not_2 (negative_overflow, not_1_out);
  and and_1 (Difference[0], not_1_out, subtractor_1bit_1_d);
  and and_2 (Difference[1], not_1_out, subtractor_1bit_2_d);
  and and_3 (Difference[2], not_1_out, subtractor_1bit_3_d);
  and and_4 (Difference[3], not_1_out, subtractor_1bit_4_d);
  and and_5 (Difference[4], not_1_out, subtractor_1bit_5_d);
  and and_6 (Difference[5], not_1_out, subtractor_1bit_6_d);
  and and_7 (Difference[6], not_1_out, subtractor_1bit_7_d);
  and and_8 (Difference[7], not_1_out, subtractor_1bit_8_d);
  and and_9 (Difference[8], not_1_out, subtractor_1bit_9_d);
  and and_10 (Difference[9], not_1_out, subtractor_1bit_10_d);
  and and_11 (Difference[10], not_1_out, subtractor_1bit_11_d);
  and and_12 (Difference[11], not_1_out, subtractor_1bit_12_d);
  and and_13 (Difference[12], not_1_out, subtractor_1bit_13_d);
  and and_14 (Difference[13], not_1_out, subtractor_1bit_14_d);
  and and_15 (Difference[14], not_1_out, subtractor_1bit_15_d);
  and and_16 (Difference[15], not_1_out, subtractor_1bit_16_d);
endmodule

module SUBTRACTOR_WITHOUT_BORROW (
  input  [15:0] B,
  input  [15:0] A,
  output [15:0] Difference,
  output negative_overflow,
  output Bout
);

  wire comparator_1_lt, not_1_out, subtractor_1bit_1_bout, subtractor_1bit_1_d, subtractor_1bit_2_bout,
       subtractor_1bit_2_d, subtractor_1bit_3_bout, subtractor_1bit_3_d, subtractor_1bit_4_bout,
       subtractor_1bit_4_d, subtractor_1bit_5_bout, subtractor_1bit_5_d, subtractor_1bit_6_bout,
       subtractor_1bit_6_d, subtractor_1bit_7_bout, subtractor_1bit_7_d, subtractor_1bit_8_bout,
       subtractor_1bit_8_d, subtractor_1bit_9_bout, subtractor_1bit_9_d, subtractor_1bit_10_bout,
       subtractor_1bit_10_d, subtractor_1bit_11_bout, subtractor_1bit_11_d, subtractor_1bit_12_bout,
       subtractor_1bit_12_d, subtractor_1bit_13_bout, subtractor_1bit_13_d, subtractor_1bit_14_bout,
       subtractor_1bit_14_d, subtractor_1bit_15_bout, subtractor_1bit_15_d, subtractor_1bit_16_d;

  Comparator #(.mode("unsigned"), .width(16)) comparator_1 (.a(A), .b(B), .lt(comparator_1_lt));  // open: gt, eq
  not not_1 (not_1_out, comparator_1_lt);
  SUBTRACTOR_1BIT subtractor_1bit_1 (
    .A(A[0]), .B(B[0]), .Bin(1'b0), .D(subtractor_1bit_1_d), .Bout(subtractor_1bit_1_bout));
  SUBTRACTOR_1BIT subtractor_1bit_2 (
    .A(A[1]), .B(B[1]), .Bin(subtractor_1bit_1_bout), .D(subtractor_1bit_2_d), .Bout(subtractor_1bit_2_bout));
  SUBTRACTOR_1BIT subtractor_1bit_3 (
    .A(A[2]), .B(B[2]), .Bin(subtractor_1bit_2_bout), .D(subtractor_1bit_3_d), .Bout(subtractor_1bit_3_bout));
  SUBTRACTOR_1BIT subtractor_1bit_4 (
    .A(A[3]), .B(B[3]), .Bin(subtractor_1bit_3_bout), .D(subtractor_1bit_4_d), .Bout(subtractor_1bit_4_bout));
  SUBTRACTOR_1BIT subtractor_1bit_5 (
    .A(A[4]), .B(B[4]), .Bin(subtractor_1bit_4_bout), .D(subtractor_1bit_5_d), .Bout(subtractor_1bit_5_bout));
  SUBTRACTOR_1BIT subtractor_1bit_6 (
    .A(A[5]), .B(B[5]), .Bin(subtractor_1bit_5_bout), .D(subtractor_1bit_6_d), .Bout(subtractor_1bit_6_bout));
  SUBTRACTOR_1BIT subtractor_1bit_7 (
    .A(A[6]), .B(B[6]), .Bin(subtractor_1bit_6_bout), .D(subtractor_1bit_7_d), .Bout(subtractor_1bit_7_bout));
  SUBTRACTOR_1BIT subtractor_1bit_8 (
    .A(A[7]), .B(B[7]), .Bin(subtractor_1bit_7_bout), .D(subtractor_1bit_8_d), .Bout(subtractor_1bit_8_bout));
  SUBTRACTOR_1BIT subtractor_1bit_9 (
    .A(A[8]), .B(B[8]), .Bin(subtractor_1bit_8_bout), .D(subtractor_1bit_9_d), .Bout(subtractor_1bit_9_bout));
  SUBTRACTOR_1BIT subtractor_1bit_10 (
    .A(A[9]), .B(B[9]), .Bin(subtractor_1bit_9_bout), .D(subtractor_1bit_10_d), .Bout(subtractor_1bit_10_bout));
  SUBTRACTOR_1BIT subtractor_1bit_11 (
    .A(A[10]), .B(B[10]), .Bin(subtractor_1bit_10_bout), .D(subtractor_1bit_11_d),
    .Bout(subtractor_1bit_11_bout));
  SUBTRACTOR_1BIT subtractor_1bit_12 (
    .A(A[11]), .B(B[11]), .Bin(subtractor_1bit_11_bout), .D(subtractor_1bit_12_d),
    .Bout(subtractor_1bit_12_bout));
  SUBTRACTOR_1BIT subtractor_1bit_13 (
    .A(A[12]), .B(B[12]), .Bin(subtractor_1bit_12_bout), .D(subtractor_1bit_13_d),
    .Bout(subtractor_1bit_13_bout));
  SUBTRACTOR_1BIT subtractor_1bit_14 (
    .A(A[13]), .B(B[13]), .Bin(subtractor_1bit_13_bout), .D(subtractor_1bit_14_d),
    .Bout(subtractor_1bit_14_bout));
  SUBTRACTOR_1BIT subtractor_1bit_15 (
    .A(A[14]), .B(B[14]), .Bin(subtractor_1bit_14_bout), .D(subtractor_1bit_15_d),
    .Bout(subtractor_1bit_15_bout));
  SUBTRACTOR_1BIT subtractor_1bit_16 (
    .A(A[15]), .B(B[15]), .Bin(subtractor_1bit_15_bout), .D(subtractor_1bit_16_d), .Bout(Bout));
  not not_2 (negative_overflow, not_1_out);
  and and_1 (Difference[0], not_1_out, subtractor_1bit_1_d);
  and and_2 (Difference[1], not_1_out, subtractor_1bit_2_d);
  and and_3 (Difference[2], not_1_out, subtractor_1bit_3_d);
  and and_4 (Difference[3], not_1_out, subtractor_1bit_4_d);
  and and_5 (Difference[4], not_1_out, subtractor_1bit_5_d);
  and and_6 (Difference[5], not_1_out, subtractor_1bit_6_d);
  and and_7 (Difference[6], not_1_out, subtractor_1bit_7_d);
  and and_8 (Difference[7], not_1_out, subtractor_1bit_8_d);
  and and_9 (Difference[8], not_1_out, subtractor_1bit_9_d);
  and and_10 (Difference[9], not_1_out, subtractor_1bit_10_d);
  and and_11 (Difference[10], not_1_out, subtractor_1bit_11_d);
  and and_12 (Difference[11], not_1_out, subtractor_1bit_12_d);
  and and_13 (Difference[12], not_1_out, subtractor_1bit_13_d);
  and and_14 (Difference[13], not_1_out, subtractor_1bit_14_d);
  and and_15 (Difference[14], not_1_out, subtractor_1bit_15_d);
  and and_16 (Difference[15], not_1_out, subtractor_1bit_16_d);
endmodule

module RAM_128K_testing (
  input  in_1,
  input  [15:0] in_2,
  input  in_3,
  input  in_4,
  input  [15:0] in_5,
  output [15:0] out_6
);

  // RAM_128K ram_128k_1: pin names not known; wires that end beside it: in_1, in_2, in_3, in_4, in_5, out_6
endmodule

module RAM_128K (
  input  [15:0] MAR_IN,
  input  MAR_SET,
  input  write_enable,
  input  allow_output,
  input  [15:0] input_value,
  output [15:0] output_value
);

  wire or_1_out;
  wire [15:0] mar_circuit_1_mar_output, ram_1_dout;

  or or_1 (or_1_out, write_enable, allow_output);
  MAR_Circuit mar_circuit_1 (.MAR_INPUT(MAR_IN), .SET_ADDRESS(MAR_SET), .MAR_OUTPUT(mar_circuit_1_mar_output));
  RAM #(.addrWidth(16), .dataWidth(16)) ram_1 (
    .addr(mar_circuit_1_mar_output), .we(write_enable), .oe(allow_output), .clk(or_1_out), .din(input_value),
    .dout(ram_1_dout));
  assign output_value = allow_output ? ram_1_dout : 16'bz;  // Controlled_Buffer controlled_buffer_1

  // Notes on the sheet:
  //   MAR_SET: pull=down
  //   MAR_IN: pull=down
  //   write_enable: pull=down
  //   allow_output: pull=down
  //   input_value: pull=down
  //   output_value: pull=down
endmodule

module CONTROL_UNIT_BEGINNING (
  input  CLK_INPUT,
  input  [15:0] IR,
  input  Carry_FLAG,
  input  Greater_Than_Flag,
  input  Equal_Flag,
  input  Zero_Flag,
  input  Undefined_Flag,
  input  Overflow_Flag,
  input  Underflow_Flag,
  input  Less_Than_Flag,
  input  stepper_reset,
  output R1_SET,
  output R1,
  output R2_SET,
  output R2,
  output R3_SET,
  output R3,
  output R4_SET,
  output R4,
  output TMP_SET,
  output ACC_SET,
  output MAR_SET,
  output ACC_ENABLE,
  output RAM_SET,
  output [3:0] opcode_to_alu,
  output IR_SET,
  output RAM_ENABLE,
  output IAR_SET,
  output IAR_ENABLE,
  output BUS_1,
  output FLAG_SET
);

  wire and_1_out, and_2_out, and_3_out, and_4_out, and_5_out, and_6_out, and_7_out, and_8_out, and_9_out,
       and_10_out, and_11_out, and_12_out, and_13_out, and_14_out, and_15_out, and_16_out, and_17_out,
       and_18_out, and_19_out, and_20_out, and_21_out, and_22_out, and_23_out, and_24_out, and_29_out,
       and_30_out, and_31_out, and_32_out, and_33_out, and_34_out, and_35_out, and_36_out, and_37_out,
       and_38_out, and_39_out, and_40_out, and_48_out, and_49_out, and_50_out, and_51_out, and_52_out,
       and_53_out, and_56_out, and_57_out, and_58_out, and_59_out, and_60_out, and_61_out, and_62_out,
       and_63_out, and_64_out, and_66_out, and_67_out, and_68_out, and_70_out, and_71_out, and_72_out,
       and_73_out, and_75_out, cpu_clock_1_clk, cpu_clock_1_clke, cpu_clock_1_clks, decoder_1_out0,
       decoder_1_out1, decoder_1_out2, decoder_1_out3, decoder_2_out0, decoder_2_out1, decoder_2_out2,
       decoder_2_out3, decoder_3_out0, decoder_3_out1, decoder_3_out2, decoder_3_out3, decoder_3_out4,
       decoder_3_out5, decoder_3_out6, decoder_3_out7, decoder_3_out8, decoder_3_out9, decoder_3_out10,
       decoder_3_out11, decoder_3_out12, decoder_3_out13, decoder_3_out14, decoder_3_out15, decoder_4_out0,
       decoder_4_out1, decoder_4_out2, decoder_4_out3, not_1_out, not_2_out, not_3_out, not_4_out, not_5_out,
       not_6_out, not_7_out, not_8_out, not_9_out, not_10_out, not_11_out, not_12_out, not_13_out,
       not_14_out, not_15_out, not_16_out, or_7_out, or_9_out, or_11_out, or_12_out, or_13_out, or_14_out,
       or_15_out, or_16_out, or_17_out, or_18_out, or_19_out, or_20_out, or_21_out, or_22_out, or_23_out,
       or_24_out, or_31_out, stepper_circuit_1_step_6;
  wire [5:0] stepper_circuit_1_step_1;

  or or_1 (R1, or_12_out, or_22_out, or_16_out);
  or or_2 (R2, or_13_out, or_16_out, or_22_out);
  or or_3 (R3, or_14_out, or_16_out, or_22_out);
  or or_4 (R4, or_15_out, or_16_out, or_22_out);
  or or_5 (BUS_1, FLAG_SET, or_7_out);
  or or_6 (ACC_ENABLE, and_56_out, or_23_out);
  or or_7 (or_7_out, and_1_out, and_38_out, stepper_circuit_1_step_1[0]);
  or or_8 (IAR_ENABLE, and_50_out, and_38_out, or_9_out);
  or or_9 (or_9_out, and_1_out, and_2_out);
  and and_1 (and_1_out, stepper_circuit_1_step_1[3], and_36_out);
  or or_10 (RAM_ENABLE, and_59_out, and_52_out, or_11_out);
  or or_11 (or_11_out, and_3_out, and_53_out, and_12_out);
  or or_12 (or_12_out, and_13_out, and_17_out);
  or or_13 (or_13_out, and_14_out, and_18_out);
  or or_14 (or_14_out, and_15_out, and_19_out);
  or or_15 (or_15_out, and_16_out, and_20_out);
  or or_16 (or_16_out, or_21_out, and_23_out);
  and and_2 (and_2_out, cpu_clock_1_clke, stepper_circuit_1_step_1[0]);
  and and_3 (and_3_out, stepper_circuit_1_step_1[1], cpu_clock_1_clke);
  and and_4 (and_4_out, IR[8], Carry_FLAG);
  and and_5 (and_5_out, IR[9], Greater_Than_Flag);
  and and_6 (and_6_out, IR[10], Equal_Flag);
  and and_7 (and_7_out, IR[11], Zero_Flag);
  and and_8 (and_8_out, IR[12], Undefined_Flag);
  and and_9 (and_9_out, IR[13], Overflow_Flag);
  and and_10 (and_10_out, IR[14], Underflow_Flag);
  and and_11 (and_11_out, IR[15], Less_Than_Flag);
  and and_12 (and_12_out, stepper_circuit_1_step_1[4], and_34_out);
  and and_13 (and_13_out, cpu_clock_1_clke, or_16_out, decoder_2_out0);
  and and_14 (and_14_out, cpu_clock_1_clke, or_16_out, decoder_2_out1);
  and and_15 (and_15_out, cpu_clock_1_clke, or_16_out, decoder_2_out2);
  and and_16 (and_16_out, cpu_clock_1_clke, or_16_out, decoder_2_out3);
  and and_17 (and_17_out, cpu_clock_1_clke, or_22_out, decoder_1_out0);
  and and_18 (and_18_out, cpu_clock_1_clke, or_22_out, decoder_1_out1);
  and and_19 (and_19_out, cpu_clock_1_clke, or_22_out, decoder_1_out2);
  and and_20 (and_20_out, cpu_clock_1_clke, or_22_out, decoder_1_out3);
  and and_21 (and_21_out, not_14_out, not_15_out, not_16_out, IR[15]);
  not not_1 (not_1_out, not_3_out);
  not not_2 (not_2_out, not_4_out);
  or or_17 (or_17_out, and_4_out, and_5_out, and_6_out);
  or or_18 (or_18_out, and_7_out, and_8_out);
  or or_19 (or_19_out, and_9_out, and_10_out, and_11_out);
  not not_3 (not_3_out, not_14_out);
  not not_4 (not_4_out, not_15_out);
  not not_5 (not_5_out, not_6_out);
  and and_22 (and_22_out, not_1_out, not_2_out, not_5_out, IR[15]);
  and and_23 (and_23_out, and_37_out, stepper_circuit_1_step_1[3]);
  or or_20 (or_20_out, or_17_out, or_18_out, or_19_out);
  and and_24 (and_24_out, stepper_circuit_1_step_1[3], and_35_out);
  not not_6 (not_6_out, not_16_out);
  and and_25 (opcode_to_alu[0], IR[8], and_21_out, stepper_circuit_1_step_1[4]);
  and and_26 (opcode_to_alu[1], IR[9], and_21_out, stepper_circuit_1_step_1[4]);
  and and_27 (opcode_to_alu[2], IR[10], and_21_out, stepper_circuit_1_step_1[4]);
  and and_28 (opcode_to_alu[3], IR[11], and_21_out, stepper_circuit_1_step_1[4]);
  not not_7 (not_7_out, not_14_out);
  not not_8 (not_8_out, not_15_out);
  not not_9 (not_9_out, not_7_out);
  and and_29 (and_29_out, not_9_out, not_8_out, not_12_out, not_11_out);
  Decoder #(.enable("false"), .select(2)) decoder_1 (
    .out0(decoder_1_out0), .out1(decoder_1_out1), .out2(decoder_1_out2), .out3(decoder_1_out3), .sel(IR[5:4]));
  and and_30 (and_30_out, stepper_circuit_1_step_1[3], and_21_out);
  and and_31 (and_31_out, stepper_circuit_1_step_1[4], and_21_out);
  not not_10 (not_10_out, not_16_out);
  not not_11 (not_11_out, IR[15]);
  not not_12 (not_12_out, not_10_out);
  not not_13 (not_13_out, and_49_out);
  Decoder #(.enable("false"), .select(2)) decoder_2 (
    .out0(decoder_2_out0), .out1(decoder_2_out1), .out2(decoder_2_out2), .out3(decoder_2_out3), .sel(IR[1:0]));
  or or_21 (or_21_out, and_57_out, and_30_out);
  and and_32 (and_32_out, stepper_circuit_1_step_1[5], and_21_out);
  not not_14 (not_14_out, IR[12]);
  not not_15 (not_15_out, IR[13]);
  not not_16 (not_16_out, IR[14]);
  or or_22 (or_22_out, and_24_out, and_31_out);
  and and_33 (and_33_out, CLK_INPUT, not_13_out);
  and and_34 (and_34_out, decoder_3_out0, and_29_out);
  and and_35 (and_35_out, decoder_3_out1, and_29_out);
  and and_36 (and_36_out, decoder_3_out2, and_29_out);
  and and_37 (and_37_out, decoder_3_out3, and_22_out);
  and and_38 (and_38_out, decoder_3_out4, and_22_out);
  and and_39 (and_39_out, decoder_3_out5, and_22_out);
  and and_40 (and_40_out, decoder_3_out6, and_22_out);
  // AND_Gate and_41 has open pins: in0=decoder_3_out7, in1=and_22_out, out=open
  // AND_Gate and_42 has open pins: in0=decoder_3_out8, in1=and_22_out, out=open
  // AND_Gate and_43 has open pins: in0=decoder_3_out9, in1=and_22_out, out=open
  // AND_Gate and_44 has open pins: in0=decoder_3_out10, in1=and_22_out, out=open
  // AND_Gate and_45 has open pins: in0=decoder_3_out11, in1=and_22_out, out=open
  // AND_Gate and_46 has open pins: in0=decoder_3_out12, in1=and_22_out, out=open
  // AND_Gate and_47 has open pins: in0=decoder_3_out13, in1=and_22_out, out=open
  and and_48 (and_48_out, decoder_3_out14, and_22_out);
  and and_49 (and_49_out, decoder_3_out15, and_22_out);
  and and_50 (and_50_out, and_38_out, stepper_circuit_1_step_1[3]);
  CPU_CLOCK cpu_clock_1 (.clkin(and_33_out), .clk(cpu_clock_1_clk), .clks(cpu_clock_1_clks), .clke(cpu_clock_1_clke));
  Decoder #(.enable("false"), .select(4)) decoder_3 (
    .out0(decoder_3_out0), .out1(decoder_3_out1), .out2(decoder_3_out2), .out3(decoder_3_out3),
    .out4(decoder_3_out4), .out5(decoder_3_out5), .out6(decoder_3_out6), .out7(decoder_3_out7),
    .out8(decoder_3_out8), .out9(decoder_3_out9), .out10(decoder_3_out10), .out11(decoder_3_out11),
    .out12(decoder_3_out12), .out13(decoder_3_out13), .out14(decoder_3_out14), .out15(decoder_3_out15),
    .sel(IR[11:8]));
  and and_51 (and_51_out, cpu_clock_1_clke, stepper_circuit_1_step_1[2]);
  STEPPER_Circuit stepper_circuit_1 (
    .reset(stepper_circuit_1_step_6), .clock_pulse(cpu_clock_1_clk), .step_7(stepper_circuit_1_step_1[1]),
    .step_2(stepper_circuit_1_step_1[2]), .step_3(stepper_circuit_1_step_1[5]),
    .step_6(stepper_circuit_1_step_6), .step_1(stepper_circuit_1_step_1[0]),
    .step_4(stepper_circuit_1_step_1[3]), .step_5(stepper_circuit_1_step_1[4]));
  or or_23 (or_23_out, and_32_out, and_58_out, and_51_out);
  and and_52 (and_52_out, stepper_circuit_1_step_1[5], and_39_out, or_20_out);
  and and_53 (and_53_out, and_36_out, stepper_circuit_1_step_1[4]);
  and and_54 (and_38_out, stepper_circuit_1_step_1[3], and_39_out);
  and and_55 (FLAG_SET, stepper_circuit_1_step_1[3], and_40_out);
  or or_24 (or_24_out, and_23_out, and_52_out);
  and and_56 (and_56_out, stepper_circuit_1_step_1[4], and_39_out);
  and and_57 (and_57_out, stepper_circuit_1_step_1[4], and_35_out);
  and and_58 (and_58_out, stepper_circuit_1_step_1[5], and_36_out);
  Decoder #(.enable("false"), .select(2)) decoder_4 (
    .out0(decoder_4_out0), .out1(decoder_4_out1), .out2(decoder_4_out2), .out3(decoder_4_out3), .sel(IR[1:0]));
  and and_59 (and_59_out, stepper_circuit_1_step_1[4], and_38_out);
  and and_60 (and_60_out, cpu_clock_1_clks, stepper_circuit_1_step_1[0]);
  and and_61 (and_61_out, decoder_4_out0, cpu_clock_1_clks, or_31_out);
  and and_62 (and_62_out, decoder_4_out1, cpu_clock_1_clks, or_31_out);
  and and_63 (and_63_out, decoder_4_out2, cpu_clock_1_clks, or_31_out);
  and and_64 (and_64_out, decoder_4_out3, cpu_clock_1_clks);
  and and_65 (TMP_SET, cpu_clock_1_clks, and_30_out);
  and and_66 (and_66_out, cpu_clock_1_clks, and_31_out);
  and and_67 (and_67_out, cpu_clock_1_clks, and_32_out);
  and and_68 (and_68_out, cpu_clock_1_clks, stepper_circuit_1_step_1[0]);
  and and_69 (RAM_SET, cpu_clock_1_clks, and_57_out);
  and and_70 (and_70_out, decoder_4_out0, or_31_out);
  and and_71 (and_71_out, decoder_4_out1, or_31_out);
  and and_72 (and_72_out, decoder_4_out2, or_31_out);
  and and_73 (and_73_out, decoder_4_out3, or_31_out);
  and and_74 (IR_SET, cpu_clock_1_clks, stepper_circuit_1_step_1[1]);
  or or_25 (R1_SET, and_61_out, and_70_out);
  or or_26 (R2_SET, and_62_out, and_71_out);
  or or_27 (ACC_SET, and_66_out, and_38_out, and_1_out, and_60_out);
  and and_75 (and_75_out, cpu_clock_1_clks, stepper_circuit_1_step_1[2]);
  or or_28 (R3_SET, and_63_out, and_72_out);
  or or_29 (R4_SET, and_64_out, and_73_out);
  or or_30 (IAR_SET, and_75_out, and_56_out, and_59_out, or_24_out, and_58_out);
  or or_31 (or_31_out, and_67_out, and_53_out, and_12_out);
  or or_32 (MAR_SET, and_68_out, and_50_out, and_38_out, and_1_out, and_24_out);

  // Notes on the sheet:
  //   Reg_B
  //   Reg_A
  //   CLK E
  //   REG B
  //   on when you
  //   run any control flow
  //   REG A
  //   program
  //   stepper 4 input
  //   stepper 5 input
  //   stepper 6 input
  //   on when you're loading and storing some data
  //   For any ALU Instruction, the format should be 1000xxxx where xxxx is the opcode of the ALU instruction you're implementing
  //   stepper 5 input
  //   IR will hold some instruction of format (type-opcode-RA-RB)
  //   this is an actual 6 step stepper. it starts from 0 to 01 to 001 to 0001 to 000001
  //   STEP 4 ANDED WITH 101
  //   CLK S
  //   REG B
  //   Reg_B_SET
endmodule

module STEPPER_Circuit (
  input  reset,
  input  clock_pulse,
  output step_7,
  output step_2,
  output step_3,
  output step_6,
  output step_1,
  output step_4,
  output step_5
);

  wire memory_bit_1bit_1_o, memory_bit_1bit_2_o, memory_bit_1bit_3_o, memory_bit_1bit_4_o,
       memory_bit_1bit_5_o, memory_bit_1bit_6_o, memory_bit_1bit_7_o, memory_bit_1bit_8_o,
       memory_bit_1bit_9_o, memory_bit_1bit_10_o, memory_bit_1bit_11_o, not_1_out, not_2_out, not_3_out,
       not_4_out, not_5_out, not_6_out, not_7_out, not_8_out, or_2_out, or_3_out;

  not not_1 (not_1_out, clock_pulse);
  or or_1 (step_1, reset, not_3_out);
  not not_2 (not_2_out, reset);
  or or_2 (or_2_out, reset, not_1_out);
  or or_3 (or_3_out, reset, clock_pulse);
  MEMORY_BIT_1BIT memory_bit_1bit_1 (.i(not_2_out), .s(or_2_out), .o(memory_bit_1bit_1_o));
  not not_3 (not_3_out, memory_bit_1bit_2_o);
  MEMORY_BIT_1BIT memory_bit_1bit_2 (.i(memory_bit_1bit_1_o), .s(or_3_out), .o(memory_bit_1bit_2_o));
  and and_1 (step_2, memory_bit_1bit_2_o, not_4_out);
  MEMORY_BIT_1BIT memory_bit_1bit_3 (.i(memory_bit_1bit_2_o), .s(or_2_out), .o(memory_bit_1bit_3_o));
  not not_4 (not_4_out, memory_bit_1bit_4_o);
  MEMORY_BIT_1BIT memory_bit_1bit_4 (.i(memory_bit_1bit_3_o), .s(or_3_out), .o(memory_bit_1bit_4_o));
  and and_2 (step_3, memory_bit_1bit_4_o, not_5_out);
  MEMORY_BIT_1BIT memory_bit_1bit_5 (.i(memory_bit_1bit_4_o), .s(or_2_out), .o(memory_bit_1bit_5_o));
  not not_5 (not_5_out, memory_bit_1bit_6_o);
  MEMORY_BIT_1BIT memory_bit_1bit_6 (.i(memory_bit_1bit_5_o), .s(or_3_out), .o(memory_bit_1bit_6_o));
  and and_3 (step_4, memory_bit_1bit_6_o, not_6_out);
  MEMORY_BIT_1BIT memory_bit_1bit_7 (.i(memory_bit_1bit_6_o), .s(or_2_out), .o(memory_bit_1bit_7_o));
  not not_6 (not_6_out, memory_bit_1bit_8_o);
  MEMORY_BIT_1BIT memory_bit_1bit_8 (.i(memory_bit_1bit_7_o), .s(or_3_out), .o(memory_bit_1bit_8_o));
  and and_4 (step_5, memory_bit_1bit_8_o, not_7_out);
  MEMORY_BIT_1BIT memory_bit_1bit_9 (.i(memory_bit_1bit_8_o), .s(or_2_out), .o(memory_bit_1bit_9_o));
  not not_7 (not_7_out, memory_bit_1bit_10_o);
  MEMORY_BIT_1BIT memory_bit_1bit_10 (.i(memory_bit_1bit_9_o), .s(or_3_out), .o(memory_bit_1bit_10_o));
  and and_5 (step_6, memory_bit_1bit_10_o, not_8_out);
  MEMORY_BIT_1BIT memory_bit_1bit_11 (.i(memory_bit_1bit_10_o), .s(or_2_out), .o(memory_bit_1bit_11_o));
  not not_8 (not_8_out, step_7);
  MEMORY_BIT_1BIT memory_bit_1bit_12 (.i(memory_bit_1bit_11_o), .s(or_3_out), .o(step_7));

  // Notes on the sheet:
  //   clock_pulse: pull=down
  //   reset: pull=down
endmodule

module MEMORY_BIT_1BIT (
  input  i,
  input  s,
  output o
);

  wire nand_1_out, nand_2_out, nand_4_out;

  nand nand_1 (nand_1_out, i, s);
  nand nand_2 (nand_2_out, nand_1_out, s);
  nand nand_3 (o, nand_1_out, nand_4_out);
  nand nand_4 (nand_4_out, o, nand_2_out);

  // Notes on the sheet:
  //   i: pull=down
  //   s: pull=down
endmodule

module test_ground (
  input  in_1,
  output out_2,
  output out_3,
  output out_4,
  output out_5,
  output out_6,
  output out_7,
  output out_8
);

  wire clock_1_out;

  Clock clock_1 (.out(clock_1_out));
  STEPPER_Circuit stepper_circuit_1 (
    .reset(out_2), .clock_pulse(clock_1_out), .step_7(out_4), .step_2(out_5), .step_3(out_8), .step_6(out_2),
    .step_1(out_3), .step_4(out_6), .step_5(out_7));
endmodule

module IAR_Circuit (
  input  [15:0] IAR_INPUT,
  input  IAR_SET,
  input  IAR_ENABLE,
  output [15:0] IAR_OUTPUT
);

  REGISTER_WITHOUT_OUTPUT register_without_output_1 (.i(IAR_INPUT), .s(IAR_SET), .e(IAR_ENABLE), .o(IAR_OUTPUT));

  // Notes on the sheet:
  //   IAR_SET: pull=down
  //   IAR_INPUT: pull=down
  //   IAR_ENABLE: pull=down
  //   IAR_OUTPUT: pull=down
endmodule

module IR_Circuit (
  input  [15:0] IR_INPUT,
  input  IR_SET,
  output [15:0] IR_OUTPUT
);

  REGISTER_WITHOUT_OUTPUT register_without_output_1 (.i(IR_INPUT), .s(IR_SET), .e(1'b1), .o(IR_OUTPUT));

  // Notes on the sheet:
  //   IR_SET: pull=down
  //   IR_INPUT: pull=down
  //   IR_OUTPUT: pull=down
endmodule

module MAR_Circuit (
  input  [15:0] MAR_INPUT,
  input  SET_ADDRESS,
  output [15:0] MAR_OUTPUT
);

  REGISTER_WITHOUT_OUTPUT register_without_output_1 (.i(MAR_INPUT), .s(SET_ADDRESS), .e(1'b1), .o(MAR_OUTPUT));

  // Notes on the sheet:
  //   SET_ADDRESS: pull=down
  //   MAR_INPUT: pull=down
  //   MAR_OUTPUT: pull=down
endmodule

module ACC_Circuit (
  input  [15:0] ACC_INPUT,
  input  ACC_SET,
  input  ACC_ENABLE,
  output [15:0] ACC_OUTPUT
);

  REGISTER_WITHOUT_OUTPUT register_without_output_1 (.i(ACC_INPUT), .s(ACC_SET), .e(ACC_ENABLE), .o(ACC_OUTPUT));

  // Notes on the sheet:
  //   ACC_SET: pull=down
  //   ACC_INPUT: pull=down
  //   ACC_ENABLE: pull=down
endmodule

module TMP_Circuit (
  input  [15:0] TMP_i,
  input  TMP_SET,
  output [15:0] TMP_o
);

  wire [15:0] controlled_buffer_1_out;

  assign controlled_buffer_1_out = TMP_SET ? TMP_i : 16'bz;  // Controlled_Buffer controlled_buffer_1
  LATCH_16BIT latch_16bit_1 (.input_to_latch(controlled_buffer_1_out), .s(TMP_SET), .latch_out(TMP_o));

  // Notes on the sheet:
  //   TMP_i: pull=down
  //   TMP_SET: pull=down
  //   TMP_o: pull=down
endmodule

module LATCH_16BIT (
  input  [15:0] input_to_latch,
  input  s,
  output [15:0] latch_out
);

  MEMORY_BIT_1BIT memory_bit_1bit_1 (.i(input_to_latch[0]), .s(s), .o(latch_out[0]));
  MEMORY_BIT_1BIT memory_bit_1bit_2 (.i(input_to_latch[1]), .s(s), .o(latch_out[1]));
  MEMORY_BIT_1BIT memory_bit_1bit_3 (.i(input_to_latch[2]), .s(s), .o(latch_out[2]));
  MEMORY_BIT_1BIT memory_bit_1bit_4 (.i(input_to_latch[3]), .s(s), .o(latch_out[3]));
  MEMORY_BIT_1BIT memory_bit_1bit_5 (.i(input_to_latch[4]), .s(s), .o(latch_out[4]));
  MEMORY_BIT_1BIT memory_bit_1bit_6 (.i(input_to_latch[5]), .s(s), .o(latch_out[5]));
  MEMORY_BIT_1BIT memory_bit_1bit_7 (.i(input_to_latch[6]), .s(s), .o(latch_out[6]));
  MEMORY_BIT_1BIT memory_bit_1bit_8 (.i(input_to_latch[7]), .s(s), .o(latch_out[7]));
  MEMORY_BIT_1BIT memory_bit_1bit_9 (.i(input_to_latch[8]), .s(s), .o(latch_out[8]));
  MEMORY_BIT_1BIT memory_bit_1bit_10 (.i(input_to_latch[9]), .s(s), .o(latch_out[9]));
  MEMORY_BIT_1BIT memory_bit_1bit_11 (.i(input_to_latch[10]), .s(s), .o(latch_out[10]));
  MEMORY_BIT_1BIT memory_bit_1bit_12 (.i(input_to_latch[11]), .s(s), .o(latch_out[11]));
  MEMORY_BIT_1BIT memory_bit_1bit_13 (.i(input_to_latch[12]), .s(s), .o(latch_out[12]));
  MEMORY_BIT_1BIT memory_bit_1bit_14 (.i(input_to_latch[13]), .s(s), .o(latch_out[13]));
  MEMORY_BIT_1BIT memory_bit_1bit_15 (.i(input_to_latch[14]), .s(s), .o(latch_out[14]));
  MEMORY_BIT_1BIT memory_bit_1bit_16 (.i(input_to_latch[15]), .s(s), .o(latch_out[15]));

  // Notes on the sheet:
  //   input_to_latch: pull=down
  //   s: pull=down
  //   latch_out: pull=down
endmodule

module CPU_ENABLES (
  input  [15:0] input_i,
  input  enable,
  output [15:0] output_o
);

  wire and_1_out, and_2_out, and_3_out, and_4_out, and_5_out, and_6_out, and_7_out, and_8_out, and_9_out,
       and_10_out, and_11_out, and_12_out, and_13_out, and_14_out, and_15_out, and_16_out;

  and and_1 (and_1_out, input_i[0], enable);
  and and_2 (and_2_out, input_i[1], enable);
  and and_3 (and_3_out, input_i[2], enable);
  and and_4 (and_4_out, input_i[3], enable);
  and and_5 (and_5_out, input_i[4], enable);
  and and_6 (and_6_out, input_i[5], enable);
  and and_7 (and_7_out, input_i[6], enable);
  and and_8 (and_8_out, input_i[7], enable);
  and and_9 (and_9_out, input_i[8], enable);
  and and_10 (and_10_out, input_i[9], enable);
  and and_11 (and_11_out, input_i[10], enable);
  and and_12 (and_12_out, input_i[11], enable);
  and and_13 (and_13_out, input_i[12], enable);
  and and_14 (and_14_out, input_i[13], enable);
  and and_15 (and_15_out, input_i[14], enable);
  and and_16 (and_16_out, input_i[15], enable);
  assign output_o[15] = enable ? and_1_out : 1'bz;  // Controlled_Buffer controlled_buffer_1
  assign output_o[1] = enable ? and_2_out : 1'bz;  // Controlled_Buffer controlled_buffer_2
  assign output_o[2] = enable ? and_3_out : 1'bz;  // Controlled_Buffer controlled_buffer_3
  assign output_o[3] = enable ? and_4_out : 1'bz;  // Controlled_Buffer controlled_buffer_4
  assign output_o[4] = enable ? and_5_out : 1'bz;  // Controlled_Buffer controlled_buffer_5
  assign output_o[5] = enable ? and_6_out : 1'bz;  // Controlled_Buffer controlled_buffer_6
  assign output_o[6] = enable ? and_7_out : 1'bz;  // Controlled_Buffer controlled_buffer_7
  assign output_o[7] = enable ? and_8_out : 1'bz;  // Controlled_Buffer controlled_buffer_8
  assign output_o[8] = enable ? and_9_out : 1'bz;  // Controlled_Buffer controlled_buffer_9
  assign output_o[9] = enable ? and_10_out : 1'bz;  // Controlled_Buffer controlled_buffer_10
  assign output_o[10] = enable ? and_11_out : 1'bz;  // Controlled_Buffer controlled_buffer_11
  assign output_o[11] = enable ? and_12_out : 1'bz;  // Controlled_Buffer controlled_buffer_12
  assign output_o[12] = enable ? and_13_out : 1'bz;  // Controlled_Buffer controlled_buffer_13
  assign output_o[13] = enable ? and_14_out : 1'bz;  // Controlled_Buffer controlled_buffer_14
  assign output_o[14] = enable ? and_15_out : 1'bz;  // Controlled_Buffer controlled_buffer_15
  assign output_o[15] = enable ? and_16_out : 1'bz;  // Controlled_Buffer controlled_buffer_16

  assign output_o[0] = output_o[15];
endmodule

module REGISTER_CPU (
  input  [15:0] i,
  input  s,
  input  e,
  output [15:0] register_output,
  output [15:0] o
);

  wire [15:0] cpu_enables_1_output_o;

  LATCH_16BIT latch_16bit_1 (.input_to_latch(i), .s(s), .latch_out(register_output));
  CPU_ENABLES cpu_enables_1 (.input_i(register_output), .enable(e), .output_o(cpu_enables_1_output_o));
  assign o = e ? cpu_enables_1_output_o : 16'bz;  // Controlled_Buffer controlled_buffer_1

  // Notes on the sheet:
  //   i: pull=down
  //   s: pull=down
  //   e: pull=down
  //   the register output simply shows us the result of a write operation without outputing it
endmodule

module REGISTER_WITHOUT_OUTPUT (
  input  [15:0] i,
  input  s,
  input  e,
  output [15:0] o
);

  wire [15:0] cpu_enables_1_output_o, latch_16bit_1_latch_out;

  LATCH_16BIT latch_16bit_1 (.input_to_latch(i), .s(s), .latch_out(latch_16bit_1_latch_out));
  CPU_ENABLES cpu_enables_1 (.input_i(latch_16bit_1_latch_out), .enable(e), .output_o(cpu_enables_1_output_o));
  assign o = e ? cpu_enables_1_output_o : 16'bz;  // Controlled_Buffer controlled_buffer_1

  // Notes on the sheet:
  //   i: pull=down
  //   s: pull=down
  //   e: pull=down
  //   o: pull=down
endmodule

module CPU_CLOCK (
  input  clkin,
  output clk,
  output clks,
  output clke
);

  wire j_k_ff_1_qn, nand_1_out;

  J_K_Flip_Flop j_k_ff_1 (.J(1'b1), .K(1'b1), .clk(clkin), .Q(clk), .Qn(j_k_ff_1_qn));  // open: preset, reset
  nand nand_1 (nand_1_out, clkin, clk);
  nand nand_2 (clke, j_k_ff_1_qn, clkin);
  not not_1 (clks, nand_1_out);
endmodule

module GENERAL_PURPOSE_REGISTERS_Rx (
  input  [15:0] Rx_INPUT,
  input  Rx_SET,
  input  Rx_ENABLE,
  output [15:0] Rx_OUTPUT
);

  REGISTER_WITHOUT_OUTPUT register_without_output_1 (.i(Rx_INPUT), .s(Rx_SET), .e(Rx_ENABLE), .o(Rx_OUTPUT));

  // Notes on the sheet:
  //   Rx_SET: pull=down
  //   Rx_INPUT: pull=down
  //   Rx_ENABLE: pull=down
endmodule

module ALU_Load_Store_CU_testing (
);

  CONTROL_UNIT_BEGINNING control_unit_beginning_1 ();  // open: CLK_INPUT, IR, Carry_FLAG, Greater_Than_Flag, Equal_Flag, Zero_Flag, Undefined_Flag, Overflow_Flag, Underflow_Flag, Less_Than_Flag, stepper_reset, R1_SET, R1, R2_SET, R2, R3_SET, R3, R4_SET, R4, TMP_SET, ACC_SET, MAR_SET, ACC_ENABLE, RAM_SET, opcode_to_alu, IR_SET, RAM_ENABLE, IAR_SET, IAR_ENABLE, BUS_1, FLAG_SET
endmodule

module BUS_1_CIRCUIT (
  input  [15:0] in_pins,
  input  BUS_1V,
  output [15:0] out_pins
);

  wire not_1_out;

  and and_1 (out_pins[15], in_pins[15], not_1_out);
  and and_2 (out_pins[14], in_pins[14], not_1_out);
  and and_3 (out_pins[13], in_pins[13], not_1_out);
  and and_4 (out_pins[12], in_pins[12], not_1_out);
  and and_5 (out_pins[11], in_pins[11], not_1_out);
  and and_6 (out_pins[10], in_pins[10], not_1_out);
  and and_7 (out_pins[9], in_pins[9], not_1_out);
  and and_8 (out_pins[8], in_pins[8], not_1_out);
  and and_9 (out_pins[7], in_pins[7], not_1_out);
  and and_10 (out_pins[6], in_pins[6], not_1_out);
  and and_11 (out_pins[5], in_pins[5], not_1_out);
  and and_12 (out_pins[4], in_pins[4], not_1_out);
  and and_13 (out_pins[2], in_pins[2], not_1_out);
  and and_14 (out_pins[3], in_pins[3], not_1_out);
  and and_15 (out_pins[1], in_pins[1], not_1_out);
  not not_1 (not_1_out, BUS_1V);
  or or_1 (out_pins[0], in_pins[0], BUS_1V);

  // Notes on the sheet:
  //   BUS_1V: pull=down
  //   in_pins: pull=down
  //   out_pins: pull=down
  //   IN PINS
  //   OUT PINS
  //   BUS 1
endmodule

module tyere (
  input  in_1
);

  wire clock_1_out, clock_2_out, cpu_clock_1_clk, cpu_clock_1_clke, cpu_clock_1_clks, or_1_out, por_1_out,
       stepper_circuit_1_step_6, tick_once_out;

  Clock clock_1 (.out(clock_1_out));
  Clock tick_once (.out(tick_once_out));
  POR por_1 (.out(por_1_out));
  Clock clock_2 (.out(clock_2_out));
  CPU_CLOCK cpu_clock_1 (.clkin(clock_1_out), .clk(cpu_clock_1_clk), .clks(cpu_clock_1_clks), .clke(cpu_clock_1_clke));
  or or_1 (or_1_out, stepper_circuit_1_step_6, tick_once_out);
  STEPPER_Circuit stepper_circuit_1 (
    .reset(or_1_out), .clock_pulse(clock_2_out), .step_6(stepper_circuit_1_step_6));  // open: step_7, step_2, step_3, step_1, step_4, step_5
endmodule

module FLAG_Register (
  input  Carry_FLAG,
  input  Greater_Than_FLAG,
  input  Equal_FLAG,
  input  Zero_FLAG,
  input  Undefined_FLAG,
  input  Overflow_FLAG,
  input  Underflow_FLAG,
  input  Less_Than_FLAG,
  input  FLAG_SET,
  output Carry,
  output Greater,
  output Equal,
  output Zero,
  output Undefined,
  output Overflow,
  output Underflow,
  output Less
);

  wire memory_bit_1bit_8_o;

  MEMORY_BIT_1BIT memory_bit_1bit_1 (.i(Carry_FLAG), .s(FLAG_SET), .o(Carry));
  MEMORY_BIT_1BIT memory_bit_1bit_2 (.i(Greater_Than_FLAG), .s(FLAG_SET), .o(Greater));
  MEMORY_BIT_1BIT memory_bit_1bit_3 (.i(Equal_FLAG), .s(FLAG_SET), .o(Equal));
  MEMORY_BIT_1BIT memory_bit_1bit_4 (.i(Zero_FLAG), .s(FLAG_SET), .o(Zero));
  MEMORY_BIT_1BIT memory_bit_1bit_5 (.i(Undefined_FLAG), .s(FLAG_SET), .o(Undefined));
  MEMORY_BIT_1BIT memory_bit_1bit_6 (.i(Overflow_FLAG), .s(FLAG_SET), .o(Overflow));
  MEMORY_BIT_1BIT memory_bit_1bit_7 (.i(Underflow_FLAG), .s(FLAG_SET), .o(Underflow));
  MEMORY_BIT_1BIT memory_bit_1bit_8 (.i(Less_Than_FLAG), .s(FLAG_SET), .o(memory_bit_1bit_8_o));
  assign Less = FLAG_SET ? memory_bit_1bit_8_o : 1'bz;  // Controlled_Buffer controlled_buffer_1

  // Notes on the sheet:
  //   Carry_FLAG: pull=down
  //   Greater_Than_FLAG: pull=down
  //   Equal_FLAG: pull=down
  //   Zero_FLAG: pull=down
  //   Undefined_FLAG: pull=down
  //   Overflow_FLAG: pull=down
  //   Underflow_FLAG: pull=down
  //   Less_Than_FLAG: pull=down
  //   FLAG_SET: pull=down
endmodule

module test_full (
);

  wire and_1_out;

  and and_1 (and_1_out, and_1_out, and_1_out);
endmodule
